// Logisim project Guia_1103.circ as structural Verilog: 1 circuit, main circuit main
module main (
  input  pulse,
  input  clr
);

  wire and_1_out, clk_out, d_ff_1_q, d_ff_1_qn, d_ff_2_q, d_ff_3_q, d_ff_3_qn, d_ff_4_q;

  Clock clk (.out(clk_out));
  D_Flip_Flop d_ff_1 (.clk(clk_out), .D(pulse), .Q(d_ff_1_q), .Qn(d_ff_1_qn), .reset(clr));  // open: preset
  D_Flip_Flop d_ff_2 (.clk(clk_out), .D(d_ff_1_q), .Q(d_ff_2_q), .reset(clr));  // open: Qn, preset
  and and_1 (and_1_out, d_ff_4_q, d_ff_3_qn, d_ff_2_q, d_ff_1_qn);
  D_Flip_Flop d_ff_3 (.clk(clk_out), .D(d_ff_2_q), .Q(d_ff_3_q), .Qn(d_ff_3_qn), .reset(clr));  // open: preset
  D_Flip_Flop d_ff_4 (.clk(clk_out), .D(d_ff_3_q), .Q(d_ff_4_q), .reset(clr));  // open: Qn, preset
  D_Flip_Flop d_ff_5 (.clk(clk_out), .D(and_1_out), .reset(clr));  // open: Q, Qn, preset
endmodule
