// Logisim project Guia_1104.circ as structural Verilog: 1 circuit, main circuit main
module main (
  input  pulse,
  input  clr,
  output out_3
);

  wire clk_out, d_ff_1_q, d_ff_1_qn, d_ff_2_q, d_ff_3_q, d_ff_4_q, or_1_out;

  Clock clk (.out(clk_out));
  D_Flip_Flop d_ff_1 (.clk(clk_out), .D(pulse), .Q(d_ff_1_q), .Qn(d_ff_1_qn), .reset(clr));  // open: preset
  or or_1 (or_1_out, d_ff_1_q, d_ff_1_qn);
  D_Flip_Flop d_ff_2 (.clk(clk_out), .D(or_1_out), .Q(d_ff_2_q), .reset(clr));  // open: Qn, preset
  and and_1 (out_3, d_ff_4_q, d_ff_3_q, d_ff_2_q, or_1_out);
  D_Flip_Flop d_ff_3 (.clk(clk_out), .D(d_ff_2_q), .Q(d_ff_3_q), .reset(clr));  // open: Qn, preset
  D_Flip_Flop d_ff_4 (.clk(clk_out), .D(d_ff_3_q), .Q(d_ff_4_q), .reset(clr));  // open: Qn, preset
endmodule
