// Logisim project Guia_1105.circ as structural Verilog: 1 circuit, main circuit main
module main (
  input  pulse,
  input  clr,
  output out_3
);

  wire and_1_out, and_2_out, clk_out, d_ff_1_q, d_ff_2_q, d_ff_2_qn, d_ff_3_q, d_ff_4_q, d_ff_4_qn,
       d_ff_5_qn, d_ff_6_q;

  Clock clk (.out(clk_out));
  D_Flip_Flop d_ff_1 (.clk(clk_out), .D(pulse), .Q(d_ff_1_q), .reset(clr));  // open: Qn, preset
  D_Flip_Flop d_ff_2 (.clk(clk_out), .D(pulse), .Q(d_ff_2_q), .Qn(d_ff_2_qn), .reset(clr));  // open: preset
  D_Flip_Flop d_ff_3 (.clk(clk_out), .D(d_ff_2_q), .Q(d_ff_3_q), .reset(clr));  // open: Qn, preset
  D_Flip_Flop d_ff_4 (.clk(clk_out), .D(d_ff_1_q), .Q(d_ff_4_q), .Qn(d_ff_4_qn), .reset(clr));  // open: preset
  and and_1 (and_1_out, d_ff_6_q, d_ff_4_qn, d_ff_1_q);
  D_Flip_Flop d_ff_5 (.clk(clk_out), .D(d_ff_3_q), .Qn(d_ff_5_qn), .reset(clr));  // open: Q, preset
  and and_2 (and_2_out, d_ff_5_qn, d_ff_3_q, d_ff_2_qn);
  D_Flip_Flop d_ff_6 (.clk(clk_out), .D(d_ff_4_q), .Q(d_ff_6_q), .reset(clr));  // open: Qn, preset
  or or_1 (out_3, and_1_out, and_2_out);
endmodule
