// Logisim project Guia_1201.circ as structural Verilog: 1 circuit, main circuit main
module main (
  input  [3:0] in_1,
  input  Address,
  input  clear,
  output [3:0] out_4
);

  wire and_1_out, Clock_out;
  wire [3:0] d_ff_4_q;

  Clock Clock (.out(Clock_out));
  and and_1 (and_1_out, Address, Clock_out);
  D_Flip_Flop d_ff_1 (.clk(and_1_out), .D(in_1[3]), .Q(d_ff_4_q[3]), .reset(clear));  // open: Qn, preset
  D_Flip_Flop d_ff_2 (.clk(and_1_out), .D(in_1[2]), .Q(d_ff_4_q[2]), .reset(clear));  // open: Qn, preset
  D_Flip_Flop d_ff_3 (.clk(and_1_out), .D(in_1[1]), .Q(d_ff_4_q[1]), .reset(clear));  // open: Qn, preset
  D_Flip_Flop d_ff_4 (.clk(and_1_out), .D(in_1[0]), .Q(d_ff_4_q[0]), .reset(clear));  // open: Qn, preset
  Multiplexer #(.width(4), .enable("false")) multiplexer_1 (.in1(d_ff_4_q), .out(out_4), .sel(Address));  // open: in0
endmodule
