// Logisim project Guia_1202.circ as structural Verilog: 2 circuits, main circuit ram1x4
module ram1x4 (
  input  [3:0] in_1,
  input  Address,
  input  r_w,
  input  clear,
  output [3:0] out_5
);

  wire and_1_out;
  wire [3:0] d_ff_4_q;

  and and_1 (and_1_out, Address, r_w);
  D_Flip_Flop d_ff_1 (.clk(and_1_out), .D(in_1[3]), .Q(d_ff_4_q[3]), .reset(clear));  // open: Qn, preset
  D_Flip_Flop d_ff_2 (.clk(and_1_out), .D(in_1[2]), .Q(d_ff_4_q[2]), .reset(clear));  // open: Qn, preset
  D_Flip_Flop d_ff_3 (.clk(and_1_out), .D(in_1[1]), .Q(d_ff_4_q[1]), .reset(clear));  // open: Qn, preset
  D_Flip_Flop d_ff_4 (.clk(and_1_out), .D(in_1[0]), .Q(d_ff_4_q[0]), .reset(clear));  // open: Qn, preset
  Multiplexer #(.width(4), .enable("false")) multiplexer_1 (.in1(d_ff_4_q), .out(out_5), .sel(Address));  // open: in0
endmodule

module ram1x8 (
  input  r_w,
  input  address,
  input  clear,
  input  [7:0] in_4,
  output [7:0] out_5
);

  ram1x4 ram1x4_1 (.in_1(in_4[7:4]), .Address(address), .r_w(r_w), .clear(clear), .out_5(out_5[7:4]));
  ram1x4 ram1x4_2 (.in_1(in_4[3:0]), .Address(address), .r_w(r_w), .clear(clear), .out_5(out_5[3:0]));
endmodule
