// Logisim project Guia_1207.circ as structural Verilog: 8 circuits, main circuit ram1x4
module ram1x4 (
  input  [3:0] in_1,
  input  Address,
  input  r_w,
  input  clear,
  output [3:0] out_5
);

  wire and_1_out;
  wire [3:0] d_ff_4_q;

  and and_1 (and_1_out, Address, r_w);
  D_Flip_Flop d_ff_1 (.clk(and_1_out), .D(in_1[3]), .Q(d_ff_4_q[3]), .reset(clear));  // open: Qn, preset
  D_Flip_Flop d_ff_2 (.clk(and_1_out), .D(in_1[2]), .Q(d_ff_4_q[2]), .reset(clear));  // open: Qn, preset
  D_Flip_Flop d_ff_3 (.clk(and_1_out), .D(in_1[1]), .Q(d_ff_4_q[1]), .reset(clear));  // open: Qn, preset
  D_Flip_Flop d_ff_4 (.clk(and_1_out), .D(in_1[0]), .Q(d_ff_4_q[0]), .reset(clear));  // open: Qn, preset
  Multiplexer #(.width(4), .enable("false")) multiplexer_1 (.in1(d_ff_4_q), .out(out_5), .sel(Address));  // open: in0
endmodule

module ram1x8 (
  input  r_w,
  input  address,
  input  clear,
  input  [7:0] in_4,
  output [7:0] out_5
);

  ram1x4 ram1x4_1 (.in_1(in_4[7:4]), .Address(address), .r_w(r_w), .clear(clear), .out_5(out_5[7:4]));
  ram1x4 ram1x4_2 (.in_1(in_4[3:0]), .Address(address), .r_w(r_w), .clear(clear), .out_5(out_5[3:0]));
endmodule

module ram2x8 (
  input  r_w,
  input  clear,
  input  address,
  input  [7:0] in_4,
  output [7:0] out_5
);

  wire not_1_out;
  wire [7:0] ram1x8_1_out_5, ram1x8_2_out_5;

  ram1x8 ram1x8_1 (.in_4(in_4), .r_w(r_w), .address(address), .clear(clear), .out_5(ram1x8_1_out_5));
  not not_1 (not_1_out, address);
  ram1x8 ram1x8_2 (.in_4(in_4), .r_w(r_w), .address(not_1_out), .clear(clear), .out_5(ram1x8_2_out_5));
  Multiplexer #(.width(8), .enable("false")) multiplexer_1 (
    .in0(ram1x8_1_out_5), .in1(ram1x8_2_out_5), .out(out_5), .sel(not_1_out));
endmodule

module ram4x8 (
  input  [1:0] in_1,
  input  r_w,
  input  clear,
  input  [7:0] in_4,
  output [7:0] out_5
);

  wire and_1_out, demultiplexer_1_out0, demultiplexer_1_out1, not_1_out;
  wire [7:0] ram2x8_1_out_5, ram2x8_2_out_5;

  Demultiplexer #(.enable("false")) demultiplexer_1 (
    .out0(demultiplexer_1_out0), .out1(demultiplexer_1_out1), .in(in_1[0]), .sel(in_1[1]));
  not not_1 (not_1_out, in_1[1]);
  and and_1 (and_1_out, not_1_out, r_w);
  ram2x8 ram2x8_1 (.in_4(in_4), .address(demultiplexer_1_out1), .r_w(r_w), .clear(clear), .out_5(ram2x8_1_out_5));
  ram2x8 ram2x8_2 (.in_4(in_4), .address(demultiplexer_1_out0), .r_w(and_1_out), .clear(clear), .out_5(ram2x8_2_out_5));
  Multiplexer #(.width(8), .enable("false")) multiplexer_1 (
    .in0(ram2x8_2_out_5), .in1(ram2x8_1_out_5), .out(out_5), .sel(in_1[1]));
endmodule

module ram8x8 (
  input  [2:0] in_1,
  input  r_w,
  input  clear,
  input  [7:0] in_4,
  output [7:0] out_5
);

  wire and_1_out, not_1_out;
  wire [1:0] demultiplexer_1_out0, demultiplexer_1_out1;
  wire [7:0] ram4x8_1_out_5, ram4x8_2_out_5;

  Demultiplexer #(.width(2), .enable("false")) demultiplexer_1 (
    .out0(demultiplexer_1_out0), .out1(demultiplexer_1_out1), .in(in_1[1:0]), .sel(in_1[2]));
  not not_1 (not_1_out, in_1[2]);
  ram4x8 ram4x8_1 (.in_4(in_4), .in_1(demultiplexer_1_out1), .r_w(r_w), .clear(clear), .out_5(ram4x8_1_out_5));
  and and_1 (and_1_out, not_1_out, r_w);
  ram4x8 ram4x8_2 (.in_4(in_4), .in_1(demultiplexer_1_out0), .r_w(and_1_out), .clear(clear), .out_5(ram4x8_2_out_5));
  Multiplexer #(.width(8), .enable("false")) multiplexer_1 (
    .in0(ram4x8_2_out_5), .in1(ram4x8_1_out_5), .out(out_5), .sel(in_1[2]));
endmodule

module ram1x16 (
  input  r_w,
  input  clear,
  input  address,
  input  [15:0] in_4,
  output [15:0] out_5
);

  ram1x8 ram1x8_1 (.in_4(in_4[15:8]), .r_w(r_w), .address(address), .clear(clear), .out_5(out_5[15:8]));
  ram1x8 ram1x8_2 (.in_4(in_4[7:0]), .r_w(r_w), .address(address), .clear(clear), .out_5(out_5[7:0]));
endmodule

module ram8x16 (
  input  r_w,
  input  clear,
  input  [15:0] in_3,
  input  [2:0] address,
  output [15:0] out_5
);

  wire demultiplexer_1_out0, demultiplexer_1_out1, demultiplexer_1_out2, demultiplexer_1_out3,
       demultiplexer_1_out4, demultiplexer_1_out5, demultiplexer_1_out6, demultiplexer_1_out7;
  wire [15:0] ram1x16_1_out_5, ram1x16_2_out_5, ram1x16_3_out_5, ram1x16_4_out_5, ram1x16_5_out_5,
       ram1x16_6_out_5, ram1x16_7_out_5, ram1x16_8_out_5;

  Demultiplexer #(.select(3), .enable("false")) demultiplexer_1 (
    .out0(demultiplexer_1_out0), .out1(demultiplexer_1_out1), .out2(demultiplexer_1_out2),
    .out3(demultiplexer_1_out3), .out4(demultiplexer_1_out4), .out5(demultiplexer_1_out5),
    .out6(demultiplexer_1_out6), .out7(demultiplexer_1_out7), .in(1'b1), .sel(address));
  ram1x16 ram1x16_1 (.address(demultiplexer_1_out7), .r_w(r_w), .clear(clear), .in_4(in_3), .out_5(ram1x16_1_out_5));
  ram1x16 ram1x16_2 (.address(demultiplexer_1_out6), .r_w(r_w), .clear(clear), .in_4(in_3), .out_5(ram1x16_2_out_5));
  ram1x16 ram1x16_3 (.address(demultiplexer_1_out4), .r_w(r_w), .clear(clear), .in_4(in_3), .out_5(ram1x16_3_out_5));
  ram1x16 ram1x16_4 (.address(demultiplexer_1_out5), .r_w(r_w), .clear(clear), .in_4(in_3), .out_5(ram1x16_4_out_5));
  ram1x16 ram1x16_5 (.address(demultiplexer_1_out3), .r_w(r_w), .clear(clear), .in_4(in_3), .out_5(ram1x16_5_out_5));
  ram1x16 ram1x16_6 (.address(demultiplexer_1_out2), .r_w(r_w), .clear(clear), .in_4(in_3), .out_5(ram1x16_6_out_5));
  ram1x16 ram1x16_7 (.address(demultiplexer_1_out0), .r_w(r_w), .clear(clear), .in_4(in_3), .out_5(ram1x16_7_out_5));
  ram1x16 ram1x16_8 (.address(demultiplexer_1_out1), .r_w(r_w), .clear(clear), .in_4(in_3), .out_5(ram1x16_8_out_5));
  Multiplexer #(.select(3), .width(16), .enable("false")) multiplexer_1 (
    .in0(ram1x16_7_out_5), .in1(ram1x16_8_out_5), .in2(ram1x16_6_out_5), .in3(ram1x16_5_out_5),
    .in4(ram1x16_3_out_5), .in5(ram1x16_4_out_5), .in6(ram1x16_2_out_5), .in7(ram1x16_1_out_5), .out(out_5),
    .sel(address));
endmodule

module ram16x16 (
  input  r_w,
  input  clear,
  input  [15:0] in_3,
  input  [3:0] address,
  output [15:0] out_5
);

  wire demultiplexer_1_out0, demultiplexer_1_out1, demultiplexer_1_out2, demultiplexer_1_out3,
       demultiplexer_1_out4, demultiplexer_1_out5, demultiplexer_1_out6, demultiplexer_1_out7,
       demultiplexer_1_out8, demultiplexer_1_out9, demultiplexer_1_out10, demultiplexer_1_out11,
       demultiplexer_1_out12, demultiplexer_1_out13, demultiplexer_1_out14, demultiplexer_1_out15;
  wire [15:0] ram1x16_1_out_5, ram1x16_2_out_5, ram1x16_3_out_5, ram1x16_4_out_5, ram1x16_5_out_5,
       ram1x16_6_out_5, ram1x16_7_out_5, ram1x16_8_out_5, ram1x16_9_out_5, ram1x16_10_out_5,
       ram1x16_11_out_5, ram1x16_12_out_5, ram1x16_13_out_5, ram1x16_14_out_5, ram1x16_15_out_5,
       ram1x16_16_out_5;

  Demultiplexer #(.select(4), .enable("false")) demultiplexer_1 (
    .out0(demultiplexer_1_out0), .out1(demultiplexer_1_out1), .out2(demultiplexer_1_out2),
    .out3(demultiplexer_1_out3), .out4(demultiplexer_1_out4), .out5(demultiplexer_1_out5),
    .out6(demultiplexer_1_out6), .out7(demultiplexer_1_out7), .out8(demultiplexer_1_out8),
    .out9(demultiplexer_1_out9), .out10(demultiplexer_1_out10), .out11(demultiplexer_1_out11),
    .out12(demultiplexer_1_out12), .out13(demultiplexer_1_out13), .out14(demultiplexer_1_out14),
    .out15(demultiplexer_1_out15), .in(1'b1), .sel(address));
  ram1x16 ram1x16_1 (.address(demultiplexer_1_out15), .r_w(r_w), .clear(clear), .in_4(in_3), .out_5(ram1x16_1_out_5));
  ram1x16 ram1x16_2 (.address(demultiplexer_1_out14), .r_w(r_w), .clear(clear), .in_4(in_3), .out_5(ram1x16_2_out_5));
  ram1x16 ram1x16_3 (.address(demultiplexer_1_out13), .r_w(r_w), .clear(clear), .in_4(in_3), .out_5(ram1x16_3_out_5));
  ram1x16 ram1x16_4 (.address(demultiplexer_1_out12), .r_w(r_w), .clear(clear), .in_4(in_3), .out_5(ram1x16_4_out_5));
  ram1x16 ram1x16_5 (.address(demultiplexer_1_out11), .r_w(r_w), .clear(clear), .in_4(in_3), .out_5(ram1x16_5_out_5));
  ram1x16 ram1x16_6 (.address(demultiplexer_1_out9), .r_w(r_w), .clear(clear), .in_4(in_3), .out_5(ram1x16_6_out_5));
  ram1x16 ram1x16_7 (.address(demultiplexer_1_out10), .r_w(r_w), .clear(clear), .in_4(in_3), .out_5(ram1x16_7_out_5));
  ram1x16 ram1x16_8 (.address(demultiplexer_1_out7), .r_w(r_w), .clear(clear), .in_4(in_3), .out_5(ram1x16_8_out_5));
  ram1x16 ram1x16_9 (.address(demultiplexer_1_out8), .r_w(r_w), .clear(clear), .in_4(in_3), .out_5(ram1x16_9_out_5));
  ram1x16 ram1x16_10 (.address(demultiplexer_1_out6), .r_w(r_w), .clear(clear), .in_4(in_3), .out_5(ram1x16_10_out_5));
  ram1x16 ram1x16_11 (.address(demultiplexer_1_out5), .r_w(r_w), .clear(clear), .in_4(in_3), .out_5(ram1x16_11_out_5));
  ram1x16 ram1x16_12 (.address(demultiplexer_1_out4), .r_w(r_w), .clear(clear), .in_4(in_3), .out_5(ram1x16_12_out_5));
  ram1x16 ram1x16_13 (.address(demultiplexer_1_out3), .r_w(r_w), .clear(clear), .in_4(in_3), .out_5(ram1x16_13_out_5));
  ram1x16 ram1x16_14 (.address(demultiplexer_1_out1), .r_w(r_w), .clear(clear), .in_4(in_3), .out_5(ram1x16_14_out_5));
  ram1x16 ram1x16_15 (.address(demultiplexer_1_out2), .r_w(r_w), .clear(clear), .in_4(in_3), .out_5(ram1x16_15_out_5));
  ram1x16 ram1x16_16 (.address(demultiplexer_1_out0), .r_w(r_w), .clear(clear), .in_4(in_3), .out_5(ram1x16_16_out_5));
  Multiplexer #(.select(4), .width(16), .enable("false")) multiplexer_1 (
    .in0(ram1x16_16_out_5), .in1(ram1x16_14_out_5), .in2(ram1x16_15_out_5), .in3(ram1x16_13_out_5),
    .in4(ram1x16_12_out_5), .in5(ram1x16_11_out_5), .in6(ram1x16_10_out_5), .in7(ram1x16_8_out_5),
    .in8(ram1x16_9_out_5), .in9(ram1x16_6_out_5), .in10(ram1x16_7_out_5), .in11(ram1x16_5_out_5),
    .in12(ram1x16_4_out_5), .in13(ram1x16_3_out_5), .in14(ram1x16_2_out_5), .in15(ram1x16_1_out_5),
    .out(out_5), .sel(address));
endmodule
