// Logisim project Guia_1301.circ as structural Verilog: 1 circuit, main circuit main
module main (
  input  clear,
  input  pulse
);

  wire j_k_ff_1_qn, j_k_ff_2_q, j_k_ff_2_qn, j_k_ff_3_q, j_k_ff_3_qn, j_k_ff_4_q, j_k_ff_4_qn, j_k_ff_5_q,
       j_k_ff_5_qn, j_k_ff_6_q, j_k_ff_6_qn;

  // Probe on j_k_ff_1_qn
  J_K_Flip_Flop j_k_ff_1 (.J(1'b1), .clk(j_k_ff_2_q), .K(1'b1), .Qn(j_k_ff_1_qn), .reset(clear));  // open: Q, preset
  // Probe on j_k_ff_2_qn
  J_K_Flip_Flop j_k_ff_2 (
    .J(1'b1), .clk(j_k_ff_3_q), .K(1'b1), .Q(j_k_ff_2_q), .Qn(j_k_ff_2_qn), .reset(clear));  // open: preset
  // Probe on j_k_ff_3_qn
  J_K_Flip_Flop j_k_ff_3 (
    .J(1'b1), .clk(j_k_ff_4_q), .K(1'b1), .Q(j_k_ff_3_q), .Qn(j_k_ff_3_qn), .reset(clear));  // open: preset
  J_K_Flip_Flop j_k_ff_4 (
    .J(1'b1), .clk(j_k_ff_5_q), .K(1'b1), .Q(j_k_ff_4_q), .Qn(j_k_ff_4_qn), .reset(clear));  // open: preset
  // Probe on j_k_ff_4_qn
  // Probe on j_k_ff_5_qn
  J_K_Flip_Flop j_k_ff_5 (
    .J(1'b1), .clk(j_k_ff_6_q), .K(1'b1), .Q(j_k_ff_5_q), .Qn(j_k_ff_5_qn), .reset(clear));  // open: preset
  J_K_Flip_Flop j_k_ff_6 (
    .J(1'b1), .clk(pulse), .K(1'b1), .Q(j_k_ff_6_q), .Qn(j_k_ff_6_qn), .reset(clear));  // open: preset
  // Probe on j_k_ff_6_qn
endmodule
