// Logisim project Guia_1302.circ as structural Verilog: 1 circuit, main circuit main
module main (
  input  clear,
  input  pulse
);

  wire j_k_ff_1_qn, j_k_ff_2_qn, j_k_ff_3_qn, j_k_ff_4_qn, j_k_ff_5_qn, j_k_ff_6_qn;

  J_K_Flip_Flop j_k_ff_1 (.J(1'b1), .clk(j_k_ff_2_qn), .K(1'b1), .Qn(j_k_ff_1_qn), .reset(clear));  // open: Q, preset
  // Probe on j_k_ff_1_qn
  // Probe on j_k_ff_2_qn
  J_K_Flip_Flop j_k_ff_2 (.J(1'b1), .clk(j_k_ff_3_qn), .K(1'b1), .Qn(j_k_ff_2_qn), .reset(clear));  // open: Q, preset
  J_K_Flip_Flop j_k_ff_3 (.J(1'b1), .clk(j_k_ff_4_qn), .K(1'b1), .Qn(j_k_ff_3_qn), .reset(clear));  // open: Q, preset
  // Probe on j_k_ff_3_qn
  // Probe on j_k_ff_4_qn
  J_K_Flip_Flop j_k_ff_4 (.J(1'b1), .clk(j_k_ff_5_qn), .K(1'b1), .Qn(j_k_ff_4_qn), .reset(clear));  // open: Q, preset
  // Probe on j_k_ff_5_qn
  J_K_Flip_Flop j_k_ff_5 (.J(1'b1), .clk(j_k_ff_6_qn), .K(1'b1), .Qn(j_k_ff_5_qn), .reset(clear));  // open: Q, preset
  // Probe on j_k_ff_6_qn
  J_K_Flip_Flop j_k_ff_6 (.J(1'b1), .clk(pulse), .K(1'b1), .Qn(j_k_ff_6_qn), .reset(clear));  // open: Q, preset
endmodule
