// Logisim project Guia_1304.circ as structural Verilog: 1 circuit, main circuit main
module main (
  input  clear,
  input  pulse
);

  wire and_1_out, j_k_ff_1_q, j_k_ff_1_qn, j_k_ff_2_q, j_k_ff_2_qn, j_k_ff_3_q, j_k_ff_3_qn, j_k_ff_4_q,
       j_k_ff_4_qn, j_k_ff_5_q, j_k_ff_5_qn, or_1_out;

  or or_1 (or_1_out, clear, and_1_out);
  and and_1 (and_1_out, j_k_ff_5_q, j_k_ff_4_qn, j_k_ff_3_q, j_k_ff_2_qn, j_k_ff_1_q);
  // Probe on j_k_ff_1_qn
  J_K_Flip_Flop j_k_ff_1 (
    .J(1'b1), .clk(j_k_ff_2_q), .K(1'b1), .Q(j_k_ff_1_q), .Qn(j_k_ff_1_qn), .reset(or_1_out));  // open: preset
  // Probe on j_k_ff_2_qn
  J_K_Flip_Flop j_k_ff_2 (
    .J(1'b1), .clk(j_k_ff_3_q), .K(1'b1), .Q(j_k_ff_2_q), .Qn(j_k_ff_2_qn), .reset(or_1_out));  // open: preset
  // Probe on j_k_ff_3_qn
  J_K_Flip_Flop j_k_ff_3 (
    .J(1'b1), .clk(j_k_ff_4_q), .K(1'b1), .Q(j_k_ff_3_q), .Qn(j_k_ff_3_qn), .reset(or_1_out));  // open: preset
  // Probe on j_k_ff_4_qn
  J_K_Flip_Flop j_k_ff_4 (
    .J(1'b1), .clk(j_k_ff_5_q), .K(1'b1), .Q(j_k_ff_4_q), .Qn(j_k_ff_4_qn), .reset(or_1_out));  // open: preset
  J_K_Flip_Flop j_k_ff_5 (
    .J(1'b1), .clk(pulse), .K(1'b1), .Q(j_k_ff_5_q), .Qn(j_k_ff_5_qn), .reset(or_1_out));  // open: preset
  // Probe on j_k_ff_5_qn
endmodule
