// Logisim project Guia_1305.circ as structural Verilog: 1 circuit, main circuit main
module main (
  input  pulse,
  input  clear
);

  wire and_1_out, t_ff_1_q, t_ff_2_q, t_ff_3_q;

  // Probe on t_ff_1_q
  T_Flip_Flop t_ff_1 (.clk(pulse), .T(and_1_out), .Q(t_ff_1_q), .reset(clear));  // open: Qn, preset
  and and_1 (and_1_out, t_ff_2_q, t_ff_3_q);
  // Probe on t_ff_2_q
  T_Flip_Flop t_ff_2 (.clk(pulse), .T(t_ff_3_q), .Q(t_ff_2_q), .reset(clear));  // open: Qn, preset
  // Probe on t_ff_3_q
  T_Flip_Flop t_ff_3 (.clk(pulse), .T(1'b1), .Q(t_ff_3_q), .reset(clear));  // open: Qn, preset
endmodule
