// Logisim project Guia_1307.circ as structural Verilog: 1 circuit, main circuit main
module main (
  input  pulse,
  input  in_2,
  input  clear
);

  wire j_k_ff_1_q, j_k_ff_2_q, j_k_ff_3_q, j_k_ff_4_q, j_k_ff_5_q, j_k_ff_6_qn, not_1_out, not_2_out,
       not_3_out, not_4_out, not_5_out, not_6_out, or_1_out;

  or or_1 (or_1_out, j_k_ff_6_qn, in_2);
  not not_1 (not_1_out, or_1_out);
  J_K_Flip_Flop j_k_ff_1 (.J(or_1_out), .clk(pulse), .K(not_1_out), .Q(j_k_ff_1_q), .reset(clear));  // open: Qn, preset
  not not_2 (not_2_out, j_k_ff_1_q);
  J_K_Flip_Flop j_k_ff_2 (
    .J(j_k_ff_1_q), .clk(pulse), .K(not_2_out), .Q(j_k_ff_2_q), .reset(clear));  // open: Qn, preset
  not not_3 (not_3_out, j_k_ff_2_q);
  J_K_Flip_Flop j_k_ff_3 (
    .J(j_k_ff_2_q), .clk(pulse), .K(not_3_out), .Q(j_k_ff_3_q), .reset(clear));  // open: Qn, preset
  J_K_Flip_Flop j_k_ff_4 (
    .J(j_k_ff_3_q), .clk(pulse), .K(not_4_out), .Q(j_k_ff_4_q), .reset(clear));  // open: Qn, preset
  not not_4 (not_4_out, j_k_ff_3_q);
  not not_5 (not_5_out, j_k_ff_4_q);
  J_K_Flip_Flop j_k_ff_5 (
    .J(j_k_ff_4_q), .clk(pulse), .K(not_5_out), .Q(j_k_ff_5_q), .reset(clear));  // open: Qn, preset
  J_K_Flip_Flop j_k_ff_6 (
    .J(j_k_ff_5_q), .clk(pulse), .K(not_6_out), .Qn(j_k_ff_6_qn), .reset(clear));  // open: Q, preset
  not not_6 (not_6_out, j_k_ff_5_q);
endmodule
