// Logisim project Guia_1403.circ as structural Verilog: 1 circuit, main circuit main
module main (
  input  load,
  input  preset_data,
  input  dt,
  input  clr
);

  wire and_1_out, clock_1_out, d_ff_1_q, d_ff_2_q, d_ff_3_q, d_ff_4_q, d_ff_5_q, or_1_out;

  Clock clock_1 (.out(clock_1_out));
  and and_1 (and_1_out, load, preset_data);
  or or_1 (or_1_out, dt, d_ff_5_q);
  // Probe on d_ff_1_q
  D_Flip_Flop d_ff_1 (.clk(clock_1_out), .D(or_1_out), .Q(d_ff_1_q), .preset(and_1_out), .reset(clr));  // open: Qn
  // Probe on d_ff_2_q
  D_Flip_Flop d_ff_2 (.clk(clock_1_out), .D(d_ff_1_q), .Q(d_ff_2_q), .reset(clr));  // open: Qn, preset
  // Probe on d_ff_3_q
  D_Flip_Flop d_ff_3 (.clk(clock_1_out), .D(d_ff_2_q), .Q(d_ff_3_q), .reset(clr));  // open: Qn, preset
  // Probe on d_ff_4_q
  D_Flip_Flop d_ff_4 (.clk(clock_1_out), .D(d_ff_3_q), .Q(d_ff_4_q), .reset(clr));  // open: Qn, preset
  // Probe on d_ff_5_q
  D_Flip_Flop d_ff_5 (.clk(clock_1_out), .D(d_ff_4_q), .Q(d_ff_5_q), .reset(clr));  // open: Qn, preset
endmodule
