// Logisim project Guia_1404.circ as structural Verilog: 1 circuit, main circuit main
module main (
  input  load,
  input  preset_data,
  input  clr,
  input  dt
);

  wire and_1_out, clock_1_out, d_ff_1_q, d_ff_1_qn, d_ff_2_q, d_ff_3_q, d_ff_4_q, d_ff_5_q, or_1_out;

  Clock clock_1 (.out(clock_1_out));
  // Probe on d_ff_1_q
  and and_1 (and_1_out, load, preset_data);
  D_Flip_Flop d_ff_1 (.clk(clock_1_out), .D(d_ff_2_q), .Q(d_ff_1_q), .Qn(d_ff_1_qn), .preset(and_1_out), .reset(clr));
  // Probe on d_ff_2_q
  D_Flip_Flop d_ff_2 (.clk(clock_1_out), .D(d_ff_3_q), .Q(d_ff_2_q), .reset(clr));  // open: Qn, preset
  // Probe on d_ff_3_q
  D_Flip_Flop d_ff_3 (.clk(clock_1_out), .D(d_ff_4_q), .Q(d_ff_3_q), .reset(clr));  // open: Qn, preset
  D_Flip_Flop d_ff_4 (.clk(clock_1_out), .D(d_ff_5_q), .Q(d_ff_4_q), .reset(clr));  // open: Qn, preset
  // Probe on d_ff_4_q
  or or_1 (or_1_out, d_ff_1_qn, dt);
  // Probe on d_ff_5_q
  D_Flip_Flop d_ff_5 (.clk(clock_1_out), .D(or_1_out), .Q(d_ff_5_q), .reset(clr));  // open: Qn, preset
endmodule
