// Logisim project Guia_1405.circ as structural Verilog: 1 circuit, main circuit main
module main (
  input  [4:0] data,
  input  ld,
  input  in_3
);

  wire and_1_out, and_2_out, and_3_out, and_4_out, and_5_out, clock_1_out, d_ff_1_q, d_ff_2_q, d_ff_3_q,
       d_ff_4_q, d_ff_5_q;

  Clock clock_1 (.out(clock_1_out));
  and and_1 (and_1_out, data[4], ld);
  and and_2 (and_2_out, data[3], ld);
  // Probe on d_ff_1_q
  D_Flip_Flop d_ff_1 (.clk(clock_1_out), .D(1'b0), .Q(d_ff_1_q), .preset(and_1_out), .reset(in_3));  // open: Qn
  and and_3 (and_3_out, data[2], ld);
  // Probe on d_ff_2_q
  D_Flip_Flop d_ff_2 (.clk(clock_1_out), .D(d_ff_1_q), .Q(d_ff_2_q), .preset(and_2_out), .reset(in_3));  // open: Qn
  // Probe on d_ff_3_q
  D_Flip_Flop d_ff_3 (.clk(clock_1_out), .D(d_ff_2_q), .Q(d_ff_3_q), .preset(and_3_out), .reset(in_3));  // open: Qn
  and and_4 (and_4_out, data[1], ld);
  // Probe on d_ff_4_q
  D_Flip_Flop d_ff_4 (.clk(clock_1_out), .D(d_ff_3_q), .Q(d_ff_4_q), .preset(and_4_out), .reset(in_3));  // open: Qn
  and and_5 (and_5_out, data[0], ld);
  // Probe on d_ff_5_q
  D_Flip_Flop d_ff_5 (.clk(clock_1_out), .D(d_ff_4_q), .Q(d_ff_5_q), .preset(and_5_out), .reset(in_3));  // open: Qn
endmodule
