// Logisim project Guia_1407.circ as structural Verilog: 1 circuit, main circuit main
module main (
  input  [5:0] data,
  input  ld,
  input  dt,
  input  clr
);

  wire and_1_out, and_2_out, and_3_out, and_4_out, and_5_out, and_6_out, clock_1_out, d_ff_1_q, d_ff_2_q,
       d_ff_3_q, d_ff_4_q, d_ff_5_q, d_ff_6_q, d_ff_6_qn, or_1_out;

  Clock clock_1 (.out(clock_1_out));
  or or_1 (or_1_out, d_ff_6_qn, dt);
  and and_1 (and_1_out, data[5], ld);
  and and_2 (and_2_out, data[4], ld);
  // Probe on d_ff_1_q
  D_Flip_Flop d_ff_1 (.clk(clock_1_out), .D(or_1_out), .Q(d_ff_1_q), .preset(and_1_out), .reset(clr));  // open: Qn
  and and_3 (and_3_out, data[3], ld);
  // Probe on d_ff_2_q
  D_Flip_Flop d_ff_2 (.clk(clock_1_out), .D(d_ff_1_q), .Q(d_ff_2_q), .preset(and_2_out), .reset(clr));  // open: Qn
  // Probe on d_ff_3_q
  D_Flip_Flop d_ff_3 (.clk(clock_1_out), .D(d_ff_2_q), .Q(d_ff_3_q), .preset(and_3_out), .reset(clr));  // open: Qn
  and and_4 (and_4_out, data[2], ld);
  // Probe on d_ff_4_q
  D_Flip_Flop d_ff_4 (.clk(clock_1_out), .D(d_ff_3_q), .Q(d_ff_4_q), .preset(and_4_out), .reset(clr));  // open: Qn
  and and_5 (and_5_out, data[1], ld);
  // Probe on d_ff_5_q
  D_Flip_Flop d_ff_5 (.clk(clock_1_out), .D(d_ff_4_q), .Q(d_ff_5_q), .preset(and_5_out), .reset(clr));  // open: Qn
  and and_6 (and_6_out, data[0], ld);
  // Probe on d_ff_6_q
  D_Flip_Flop d_ff_6 (.clk(clock_1_out), .D(d_ff_5_q), .Q(d_ff_6_q), .Qn(d_ff_6_qn), .preset(and_6_out), .reset(clr));
endmodule
