// Logisim project Guia_1701.circ as structural Verilog: 1 circuit, main circuit main
module main (
  input  \event ,
  input  clear
);

  wire and_1_out, and_2_out, and_3_out, and_4_out, clock_out, d_ff_1_q, d_ff_1_qn, d_ff_2_q, not_1_out,
       or_1_out, or_2_out;

  not not_1 (not_1_out, \event );
  Clock clock (.out(clock_out));
  and and_1 (and_1_out, d_ff_1_q, not_1_out);
  and and_2 (and_2_out, \event , d_ff_2_q);
  or or_1 (or_1_out, and_1_out, and_2_out);
  D_Flip_Flop d_ff_1 (.clk(clock_out), .D(or_1_out), .Q(d_ff_1_q), .Qn(d_ff_1_qn), .reset(clear));  // open: preset
  and and_3 (and_3_out, d_ff_1_qn, \event );
  and and_4 (and_4_out, d_ff_2_q, not_1_out);
  or or_2 (or_2_out, and_3_out, and_4_out);
  D_Flip_Flop d_ff_2 (.clk(clock_out), .D(or_2_out), .Q(d_ff_2_q), .reset(clear));  // open: Qn, preset
endmodule
