// Logisim project Guia_1702.circ as structural Verilog: 1 circuit, main circuit main
module main (
  input  \event ,
  input  clear
);

  wire and_1_out, and_2_out, and_3_out, and_4_out, clock_out, j_k_ff_1_q, j_k_ff_1_qn, j_k_ff_2_q,
       j_k_ff_2_qn;

  Clock clock (.out(clock_out));
  and and_1 (and_1_out, \event , j_k_ff_2_q);
  and and_2 (and_2_out, j_k_ff_2_qn, \event );
  J_K_Flip_Flop j_k_ff_1 (
    .J(and_1_out), .clk(clock_out), .K(and_2_out), .Q(j_k_ff_1_q), .Qn(j_k_ff_1_qn), .reset(clear));  // open: preset
  J_K_Flip_Flop j_k_ff_2 (
    .J(and_3_out), .clk(clock_out), .K(and_4_out), .Q(j_k_ff_2_q), .Qn(j_k_ff_2_qn), .reset(clear));  // open: preset
  and and_3 (and_3_out, j_k_ff_1_qn, \event );
  and and_4 (and_4_out, j_k_ff_1_q, \event );
endmodule
