// Logisim project Guia_1703.circ as structural Verilog: 1 circuit, main circuit main
module main (
  input  \event ,
  input  clear
);

  wire and_1_out, and_2_out, clock_out, j_k_ff_1_q, j_k_ff_2_q, not_1_out, xor_1_out;

  Clock clock (.out(clock_out));
  and and_1 (and_1_out, \event , xor_1_out);
  xor xor_1 (xor_1_out, j_k_ff_1_q, j_k_ff_2_q);
  J_K_Flip_Flop j_k_ff_1 (
    .J(and_1_out), .clk(clock_out), .K(and_1_out), .Q(j_k_ff_1_q), .reset(clear));  // open: Qn, preset
  not not_1 (not_1_out, xor_1_out);
  J_K_Flip_Flop j_k_ff_2 (
    .J(and_2_out), .clk(clock_out), .K(and_2_out), .Q(j_k_ff_2_q), .reset(clear));  // open: Qn, preset
  and and_2 (and_2_out, \event , not_1_out);
endmodule
