// Logisim project Guia_1704.circ as structural Verilog: 1 circuit, main circuit main
module main (
  input  clear,
  output [2:0] out_2
);

  wire clock_out;

  Clock clock (.out(clock_out));
  T_Flip_Flop t_ff_1 (.clk(clock_out), .T(1'b1), .Q(out_2[0]), .reset(clear));  // open: Qn, preset
  T_Flip_Flop t_ff_2 (.clk(out_2[0]), .T(1'b1), .Q(out_2[1]), .reset(clear));  // open: Qn, preset
  T_Flip_Flop t_ff_3 (.clk(out_2[1]), .T(1'b1), .Q(out_2[2]), .reset(clear));  // open: Qn, preset
endmodule
