// Logisim project Guia_1705.circ as structural Verilog: 1 circuit, main circuit main
module main (
  input  clear,
  output [2:0] out_2
);

  wire clock_out, t_ff_1_qn, t_ff_2_qn;

  Clock clock (.out(clock_out));
  T_Flip_Flop t_ff_1 (.clk(clock_out), .T(1'b1), .Q(out_2[0]), .Qn(t_ff_1_qn), .reset(clear));  // open: preset
  T_Flip_Flop t_ff_2 (.clk(t_ff_1_qn), .T(1'b1), .Q(out_2[1]), .Qn(t_ff_2_qn), .reset(clear));  // open: preset
  T_Flip_Flop t_ff_3 (.clk(t_ff_2_qn), .T(1'b1), .Qn(out_2[2]), .reset(clear));  // open: Q, preset
endmodule
