// Logisim project guia0401.circ as structural Verilog: 5 circuits, main circuit main
module main (
  input  x,
  input  y,
  input  z,
  output Result_A
);

  wire not_1_out, not_2_out, not_3_out, or_1_out;

  not not_1 (not_1_out, x);
  not not_2 (not_2_out, z);
  not not_3 (not_3_out, or_1_out);
  or or_1 (or_1_out, y, not_2_out);
  and and_1 (Result_A, not_1_out, not_3_out);

  // Notes on the sheet:
  //   Atividade 1 letra a
endmodule

module letra_b (
  input  x,
  input  y,
  input  z,
  output Result_B
);

  wire nor_1_out, not_1_out;

  not not_1 (not_1_out, x);
  nor nor_1 (nor_1_out, not_1_out, y);
  and and_1 (Result_B, nor_1_out, z);

  // Notes on the sheet:
  //   Atividade 1 letra b
endmodule

module letra_c (
  input  x,
  input  y,
  input  z,
  output Result_C
);

  wire nand_1_out, not_1_out, not_2_out, not_3_out;

  not not_1 (not_1_out, x);
  not not_2 (not_2_out, y);
  not not_3 (not_3_out, z);
  nand nand_1 (nand_1_out, not_1_out, not_2_out);
  and and_1 (Result_C, nand_1_out, not_3_out);

  // Notes on the sheet:
  //   Atividade 1 letra c
endmodule

module letra_d (
  input  x,
  input  y,
  input  z,
  output Result_D
);

  wire nand_1_out, not_1_out;

  not not_1 (not_1_out, y);
  nand nand_1 (nand_1_out, x, not_1_out);
  and and_1 (Result_D, nand_1_out, z);

  // Notes on the sheet:
  //   Atividade 1 letra d
endmodule

module letra_e (
  input  x,
  input  y,
  input  z,
  output Result_E
);

  wire nor_1_out, not_1_out, not_2_out, not_3_out, or_1_out;

  not not_1 (not_1_out, z);
  not not_2 (not_2_out, x);
  not not_3 (not_3_out, y);
  or or_1 (or_1_out, not_2_out, not_3_out);
  nor nor_1 (nor_1_out, y, not_1_out);
  and and_1 (Result_E, or_1_out, nor_1_out);

  // Notes on the sheet:
  //   Atividade 1 letra e
endmodule
