// Logisim project guia0402.circ as structural Verilog: 5 circuits, main circuit main
module main (
  input  x,
  input  y,
  output out_3,
  output out_4
);

  wire nor_1_out, not_1_out, not_2_out, not_3_out;

  not not_1 (not_1_out, x);
  nor nor_1 (nor_1_out, x, y);
  not not_2 (not_2_out, x);
  not not_3 (not_3_out, y);
  and and_1 (out_3, not_1_out, nor_1_out);
  and and_2 (out_4, not_2_out, not_3_out);

  // Notes on the sheet:
  //   Atividade 2 letra a) x'.(x+y)
  //   Atividade 2 letra a resultado) x' . y'
endmodule

module letrab (
  input  x,
  input  y,
  output out_3,
  output out_4
);

  wire and_1_out, not_1_out, not_2_out, or_1_out;

  not not_1 (not_1_out, y);
  or or_1 (or_1_out, x, not_1_out);
  not not_2 (not_2_out, x);
  and and_1 (and_1_out, not_2_out, not_1_out);
  or or_2 (out_3, or_1_out, and_1_out);
  or or_3 (out_4, x, not_1_out);

  // Notes on the sheet:
  //   Atividade 2 letra b resultado) x+y'
  //   Atividade 2 letra b) (x+y')+(x'+y')
endmodule

module letra_c (
  input  x,
  input  y,
  output out_3,
  output out_4
);

  wire nand_1_out, not_1_out, or_1_out;

  nand nand_1 (nand_1_out, x, not_1_out);
  not not_1 (not_1_out, y);
  or or_1 (or_1_out, x, y);
  and and_1 (out_3, nand_1_out, or_1_out);

  assign out_4 = y;

  // Notes on the sheet:
  //   Atividade 2 letra c) (x.y')'.(x+y)
  //   Atividade 2 letra c resultado) y
endmodule

module letra_d (
  input  x,
  input  y,
  output out_3,
  output out_4
);

  wire nand_1_out, nor_1_out, not_1_out, not_2_out;

  not not_1 (not_1_out, y);
  not not_2 (not_2_out, x);
  nand nand_1 (nand_1_out, x, not_1_out);
  nor nor_1 (nor_1_out, x, not_1_out);
  or or_1 (out_4, not_2_out, y);
  or or_2 (out_3, nand_1_out, nor_1_out);

  // Notes on the sheet:
  //   Atividade 2 letra d) (x.y')' + (x+y')'
  //   Atividade 2 letra d resultado) x'+y
endmodule

module letrae (
  input  x,
  input  y,
  output out_3,
  output out_4
);

  wire nor_1_out, not_1_out, not_2_out, not_3_out, or_1_out;

  not not_1 (not_1_out, x);
  or or_1 (or_1_out, not_1_out, y);
  nor nor_1 (nor_1_out, x, not_2_out);
  not not_2 (not_2_out, y);
  not not_3 (not_3_out, x);
  and and_1 (out_4, not_3_out, y);
  and and_2 (out_3, or_1_out, nor_1_out);

  // Notes on the sheet:
  //   Atividade 2 letra e resultado) y . x'
  //   Atividade 2 letra e) (y+x') . (y'+x)'
endmodule
