// Logisim project guia0406.circ as structural Verilog: 1 circuit, main circuit main
module main (
  input  x,
  input  y,
  input  z,
  output out_4
);

  wire not_1_out, not_2_out, or_1_out, or_2_out;

  not not_1 (not_1_out, x);
  or or_1 (or_1_out, not_1_out, y, z);
  not not_2 (not_2_out, y);
  and and_1 (out_4, or_1_out, or_2_out);
  or or_2 (or_2_out, x, not_2_out, z);
endmodule
