// Logisim project guia0502.circ as structural Verilog: 4 circuits, main circuit main
module main (
  input  a,
  input  b,
  output out_3
);

  wire nand_function_out_3, normal_function_out_3;

  normalFunction normal_function (.a(a), .b(b), .out_3(normal_function_out_3));
  nandFunction nand_function (.a(a), .b(b), .out_3(nand_function_out_3));
  xnor xnor_1 (out_3, normal_function_out_3, nand_function_out_3);
endmodule

module normalFunction (
  input  a,
  input  b,
  output out_3
);

  wire not_1_out;

  not not_1 (not_1_out, a);
  or or_1 (out_3, not_1_out, b);
endmodule

module nandFunction (
  input  a,
  input  b,
  output out_3
);

  wire notnand_1_out_2;

  nand nand_1 (out_3, a, notnand_1_out_2);
  notNand notnand_1 (.in_1(b), .out_2(notnand_1_out_2));
endmodule

module notNand (
  input  in_1,
  output out_2
);

  nand nand_1 (out_2, in_1, in_1);
endmodule
