// Logisim project guia0503.circ as structural Verilog: 4 circuits, main circuit main
module main (
  input  a,
  input  b,
  output out_3
);

  wire nor_function_out_3, normal_function_out_3;

  normalFunction normal_function (.a(a), .b(b), .out_3(normal_function_out_3));
  norFunction nor_function (.a(a), .b(b), .out_3(nor_function_out_3));
  xnor xnor_1 (out_3, normal_function_out_3, nor_function_out_3);
endmodule

module normalFunction (
  input  a,
  input  b,
  output out_3
);

  wire not_1_out;

  not not_1 (not_1_out, b);
  nor nor_1 (out_3, a, not_1_out);
endmodule

module norFunction (
  input  a,
  input  b,
  output out_3
);

  wire not_nor_out_2;

  notNor not_nor (.in_1(b), .out_2(not_nor_out_2));
  nor nor_1 (out_3, a, not_nor_out_2);
endmodule

module notNor (
  input  in_1,
  output out_2
);

  nor nor_1 (out_2, in_1, in_1);
endmodule
