// Logisim project guia0504.circ as structural Verilog: 4 circuits, main circuit main
module main (
  input  a,
  input  b,
  output out_3
);

  wire nandfunction_1_out_3, normalFunction_out_3;

  normalFunction normalFunction (.a(a), .b(b), .out_3(normalFunction_out_3));
  nandFunction nandfunction_1 (.a(a), .b(b), .out_3(nandfunction_1_out_3));
  xnor xnor_1 (out_3, normalFunction_out_3, nandfunction_1_out_3);
endmodule

module normalFunction (
  input  a,
  input  b,
  output out_3
);

  wire not_1_out;

  nand nand_1 (out_3, a, not_1_out);
  not not_1 (not_1_out, b);
endmodule

module notNand (
  input  in_1,
  output out_2
);

  nand nand_1 (out_2, in_1, in_1);
endmodule

module nandFunction (
  input  a,
  input  b,
  output out_3
);

  wire not_nand_out_2;

  nand nand_1 (out_3, a, not_nand_out_2);
  notNand not_nand (.in_1(b), .out_2(not_nand_out_2));
endmodule
