// Logisim project guia0505.circ as structural Verilog: 4 circuits, main circuit main
module main (
  input  a,
  input  b,
  output out_3
);

  wire nor_function_out_3, normal_function_out_3;

  normalFunction normal_function (.a(a), .b(b), .out_3(normal_function_out_3));
  norFunction nor_function (.a(a), .b(b), .out_3(nor_function_out_3));
  xnor xnor_1 (out_3, normal_function_out_3, nor_function_out_3);
endmodule

module normalFunction (
  input  a,
  input  b,
  output out_3
);

  xor xor_1 (out_3, a, b);
endmodule

module norFunction (
  input  a,
  input  b,
  output out_3
);

  wire and_nor_out_3, nor_2_out;

  andNor and_nor (.in_1(a), .in_2(b), .out_3(and_nor_out_3));
  nor nor_1 (out_3, and_nor_out_3, nor_2_out);
  nor nor_2 (nor_2_out, a, b);
endmodule

module andNor (
  input  in_1,
  input  in_2,
  output out_3
);

  wire nor_1_out, nor_2_out;

  nor nor_1 (nor_1_out, in_1, in_1);
  nor nor_2 (nor_2_out, in_2, in_2);
  nor nor_3 (out_3, nor_1_out, nor_2_out);
endmodule
