// Logisim project guia0506.circ as structural Verilog: 3 circuits, main circuit main
module main (
  input  a,
  input  b,
  output out_3
);

  wire nand_function_out_3, normal_function_out_3;

  normalFunction normal_function (.a(a), .b(b), .out_3(normal_function_out_3));
  normalFunction nand_function (.a(a), .b(b), .out_3(nand_function_out_3));
  xnor xnor_1 (out_3, normal_function_out_3, nand_function_out_3);
endmodule

module normalFunction (
  input  a,
  input  b,
  output out_3
);

  xnor xnor_1 (out_3, a, b);
endmodule

module nandFunction (
  input  a,
  input  b,
  output not_nand
);

  wire and_1_out, nand_1_out, nand_2_out, nand_3_out;

  nand nand_1 (nand_1_out, a, and_1_out);
  and and_1 (and_1_out, a, b);
  nand nand_2 (nand_2_out, and_1_out, b);
  nand nand_3 (nand_3_out, nand_1_out, nand_2_out);
  nand nand_4 (not_nand, nand_3_out, nand_3_out);
endmodule
