// Logisim project guia0507.circ as structural Verilog: 3 circuits, main circuit main
module main (
  input  a,
  input  b,
  output out_3
);

  wire nor_function_out_3, normal_function_out_3;

  normalFunction normal_function (.a(a), .b(b), .out_3(normal_function_out_3));
  norFunction nor_function (.a(a), .b(b), .out_3(nor_function_out_3));
  xnor xnor_1 (out_3, normal_function_out_3, nor_function_out_3);
endmodule

module normalFunction (
  input  a,
  input  b,
  output out_3
);

  wire not_1_out, not_2_out;

  not not_1 (not_1_out, a);
  not not_2 (not_2_out, b);
  xnor xnor_1 (out_3, not_1_out, not_2_out);
endmodule

module norFunction (
  input  a,
  input  b,
  output out_3
);

  wire nor_1_out, nor_2_out, nor_3_out;

  nor nor_1 (nor_1_out, a, b);
  nor nor_2 (nor_2_out, a, nor_1_out);
  nor nor_3 (nor_3_out, nor_1_out, b);
  nor nor_4 (out_3, nor_2_out, nor_3_out);
endmodule
