// Logisim project guia0508.circ as structural Verilog: 3 circuits, main circuit main
module main (
  input  a,
  input  b,
  output out_3
);

  wire nand_function_out_3, normal_function_out_3;

  normalFunction normal_function (.a(a), .b(b), .out_3(normal_function_out_3));
  nandFunction nand_function (.a(a), .b(b), .out_3(nand_function_out_3));
  xnor xnor_1 (out_3, normal_function_out_3, nand_function_out_3);
endmodule

module normalFunction (
  input  a,
  input  b,
  output out_3
);

  wire not_1_out, not_2_out;

  not not_1 (not_1_out, a);
  not not_2 (not_2_out, b);
  or or_1 (out_3, not_1_out, not_2_out);
endmodule

module nandFunction (
  input  a,
  input  b,
  output out_3
);

  nand nand_1 (out_3, a, b);
endmodule
