// Logisim project guia0601.circ as structural Verilog: 15 circuits, main circuit functionA
module functionA (
  input  in_1,
  input  in_2,
  input  in_3,
  output out_4
);

  wire and_1_out, and_2_out, and_3_out, not_1_out, not_2_out;

  not not_1 (not_1_out, in_1);
  not not_2 (not_2_out, in_2);
  and and_1 (and_1_out, not_1_out, not_2_out, in_3);
  and and_2 (and_2_out, in_1, not_2_out, in_3);
  and and_3 (and_3_out, in_1, in_2, in_3);
  or or_1 (out_4, and_1_out, and_2_out, and_3_out);
endmodule

module minimizedA (
  input  in_1,
  input  in_2,
  input  in_3,
  output out_4
);

  wire and_1_out, and_2_out, not_1_out;

  and and_1 (and_1_out, in_1, in_3);
  not not_1 (not_1_out, in_2);
  and and_2 (and_2_out, not_1_out, in_3);
  or or_1 (out_4, and_1_out, and_2_out);
endmodule

module letraA (
  input  x,
  input  y,
  input  z,
  output out_4
);

  wire functiona_1_out_4, minimizeda_1_out_4;

  functionA functiona_1 (.in_1(x), .in_2(y), .in_3(z), .out_4(functiona_1_out_4));
  minimizedA minimizeda_1 (.in_1(x), .in_2(y), .in_3(z), .out_4(minimizeda_1_out_4));
  xnor xnor_1 (out_4, functiona_1_out_4, minimizeda_1_out_4);

  // Notes on the sheet:
  //   Letra A
endmodule

module functionB (
  input  in_1,
  input  in_2,
  input  in_3,
  output out_4
);

  wire and_1_out, and_2_out, and_3_out, not_1_out, not_2_out, not_3_out;

  not not_1 (not_1_out, in_2);
  not not_2 (not_2_out, in_3);
  not not_3 (not_3_out, in_1);
  and and_1 (and_1_out, not_3_out, not_1_out, not_2_out);
  and and_2 (and_2_out, in_1, not_1_out, not_2_out);
  and and_3 (and_3_out, in_1, in_2, not_2_out);
  or or_1 (out_4, and_1_out, and_2_out, and_3_out);
endmodule

module minimizedB (
  input  in_1,
  input  in_2,
  input  in_3,
  output out_4
);

  wire and_1_out, and_2_out, not_1_out, not_2_out;

  not not_1 (not_1_out, in_2);
  not not_2 (not_2_out, in_3);
  and and_1 (and_1_out, in_1, in_2, not_2_out);
  or or_1 (out_4, and_1_out, and_2_out);
  and and_2 (and_2_out, not_1_out, not_2_out);
endmodule

module letraB (
  input  x,
  input  y,
  input  z,
  output out_4
);

  wire functionb_1_out_4, minimizedb_1_out_4;

  functionB functionb_1 (.in_1(x), .in_2(y), .in_3(z), .out_4(functionb_1_out_4));
  minimizedB minimizedb_1 (.in_1(x), .in_2(y), .in_3(z), .out_4(minimizedb_1_out_4));
  xnor xnor_1 (out_4, functionb_1_out_4, minimizedb_1_out_4);

  // Notes on the sheet:
  //   Letra B
endmodule

module functionC (
  input  x,
  input  y,
  input  z,
  output u
);

  wire and_1_out, and_2_out, and_3_out, and_4_out, not_1_out, not_2_out, not_3_out, not_4_out, not_5_out,
       not_6_out;

  not not_1 (not_1_out, x);
  not not_2 (not_2_out, y);
  not not_3 (not_3_out, x);
  not not_4 (not_4_out, z);
  not not_5 (not_5_out, x);
  not not_6 (not_6_out, z);
  and and_1 (and_1_out, not_1_out, not_2_out, z);
  and and_2 (and_2_out, not_3_out, y, not_4_out);
  and and_3 (and_3_out, not_5_out, y, z);
  and and_4 (and_4_out, x, y, not_6_out);
  or or_1 (u, and_1_out, and_2_out, and_3_out, and_4_out);
endmodule

module minimizedC (
  input  x,
  input  y,
  input  z,
  output u
);

  wire and_1_out, and_2_out, and_3_out, not_1_out, not_2_out, not_3_out;

  not not_1 (not_1_out, x);
  not not_2 (not_2_out, x);
  not not_3 (not_3_out, z);
  and and_1 (and_1_out, not_1_out, z);
  and and_2 (and_2_out, not_2_out, z);
  and and_3 (and_3_out, y, not_3_out);
  or or_1 (u, and_1_out, and_2_out, and_3_out);
endmodule

module letraC (
  input  x,
  input  y,
  input  z,
  output out_4
);

  wire functionc_1_u, minimizedc_1_u;

  functionC functionc_1 (.x(x), .y(y), .z(z), .u(functionc_1_u));
  minimizedC minimizedc_1 (.x(x), .y(y), .z(z), .u(minimizedc_1_u));
  xnor xnor_1 (out_4, functionc_1_u, minimizedc_1_u);

  // Notes on the sheet:
  //   Letra C
endmodule

module functionD (
  input  x,
  input  y,
  input  z,
  output s
);

  wire and_1_out, and_2_out, and_3_out, and_4_out, not_1_out, not_2_out, not_3_out, not_4_out, not_5_out,
       not_6_out;

  not not_1 (not_1_out, x);
  not not_2 (not_2_out, y);
  not not_3 (not_3_out, x);
  not not_4 (not_4_out, z);
  not not_5 (not_5_out, y);
  not not_6 (not_6_out, z);
  and and_1 (and_1_out, not_1_out, not_2_out, z);
  and and_2 (and_2_out, not_3_out, y, not_4_out);
  and and_3 (and_3_out, x, not_5_out, z);
  and and_4 (and_4_out, x, y, not_6_out);
  or or_1 (s, and_1_out, and_2_out, and_3_out, and_4_out);
endmodule

module minimizedD (
  input  x,
  input  y,
  input  z,
  output s
);

  wire and_1_out, and_2_out, not_1_out, not_2_out;

  not not_1 (not_1_out, y);
  not not_2 (not_2_out, z);
  and and_1 (and_1_out, not_1_out, z);
  and and_2 (and_2_out, y, not_2_out);
  or or_1 (s, and_1_out, and_2_out);
endmodule

module letraD (
  input  x,
  input  y,
  input  z,
  output out_4
);

  wire functiond_1_s, minimizedd_1_s;

  functionD functiond_1 (.x(x), .y(y), .z(z), .s(functiond_1_s));
  minimizedD minimizedd_1 (.x(x), .y(y), .z(z), .s(minimizedd_1_s));
  xnor xnor_1 (out_4, functiond_1_s, minimizedd_1_s);

  // Notes on the sheet:
  //   Letra D
endmodule

module functionE (
  input  x,
  input  y,
  input  z,
  output s
);

  wire and_1_out, and_2_out, and_3_out, and_4_out, not_1_out, not_2_out, not_3_out, not_4_out, not_5_out,
       not_6_out, not_7_out;

  not not_1 (not_1_out, x);
  not not_2 (not_2_out, y);
  not not_3 (not_3_out, z);
  not not_4 (not_4_out, x);
  not not_5 (not_5_out, z);
  not not_6 (not_6_out, y);
  not not_7 (not_7_out, z);
  and and_1 (and_1_out, not_1_out, not_2_out, not_3_out);
  and and_2 (and_2_out, not_4_out, y, not_5_out);
  and and_3 (and_3_out, x, not_6_out, not_7_out);
  and and_4 (and_4_out, x, y, z);
  or or_1 (s, and_1_out, and_2_out, and_3_out, and_4_out);
endmodule

module minimizedE (
  input  x,
  input  y,
  input  z,
  output s
);

  wire and_1_out, and_2_out, and_3_out, not_1_out, not_2_out, not_3_out, not_4_out;

  not not_1 (not_1_out, y);
  not not_2 (not_2_out, z);
  not not_3 (not_3_out, x);
  not not_4 (not_4_out, z);
  and and_1 (and_1_out, not_1_out, not_2_out);
  and and_2 (and_2_out, x, y, z);
  and and_3 (and_3_out, not_3_out, y, not_4_out);
  or or_1 (s, and_1_out, and_2_out, and_3_out);
endmodule

module letraE (
  input  x,
  input  y,
  input  z,
  output out_4
);

  wire functione_1_s, minimizede_1_s;

  functionE functione_1 (.x(x), .y(y), .z(z), .s(functione_1_s));
  minimizedE minimizede_1 (.x(x), .y(y), .z(z), .s(minimizede_1_s));
  xnor xnor_1 (out_4, functione_1_s, minimizede_1_s);

  // Notes on the sheet:
  //   Letra E
endmodule
