// Logisim project guia0602.circ as structural Verilog: 15 circuits, main circuit functionA
module functionA (
  input  a,
  input  b,
  input  c,
  output s
);

  wire not_1_out, not_2_out, not_3_out, not_4_out, not_5_out, not_6_out, or_1_out, or_2_out, or_3_out;

  not not_1 (not_1_out, c);
  not not_2 (not_2_out, a);
  not not_3 (not_3_out, c);
  not not_4 (not_4_out, a);
  not not_5 (not_5_out, b);
  not not_6 (not_6_out, c);
  or or_1 (or_1_out, a, b, not_1_out);
  or or_2 (or_2_out, not_2_out, b, not_3_out);
  or or_3 (or_3_out, not_4_out, not_5_out, not_6_out);
  and and_1 (s, or_1_out, or_2_out, or_3_out);
endmodule

module minimizedA (
  input  a,
  input  b,
  input  c,
  output s
);

  wire not_1_out, not_2_out, not_3_out, or_1_out, or_2_out;

  not not_1 (not_1_out, c);
  not not_2 (not_2_out, a);
  not not_3 (not_3_out, c);
  or or_1 (or_1_out, b, not_1_out);
  or or_2 (or_2_out, not_2_out, not_3_out);
  and and_1 (s, or_1_out, or_2_out);
endmodule

module letraA (
  input  a,
  input  b,
  input  c,
  output out_4
);

  wire functiona_1_s, minimizeda_1_s;

  functionA functiona_1 (.a(a), .b(b), .c(c), .s(functiona_1_s));
  minimizedA minimizeda_1 (.a(a), .b(b), .c(c), .s(minimizeda_1_s));
  xnor xnor_1 (out_4, functiona_1_s, minimizeda_1_s);

  // Notes on the sheet:
  //   Letra A
endmodule

module functionB (
  input  a,
  input  b,
  input  c,
  output s
);

  wire not_1_out, not_2_out, not_3_out, or_1_out, or_2_out, or_3_out;

  not not_1 (not_1_out, a);
  not not_2 (not_2_out, a);
  not not_3 (not_3_out, b);
  or or_1 (or_1_out, a, b, c);
  or or_2 (or_2_out, not_1_out, b, c);
  or or_3 (or_3_out, not_2_out, not_3_out, c);
  and and_1 (s, or_1_out, or_2_out, or_3_out);
endmodule

module minimizedB (
  input  a,
  input  b,
  input  c,
  output s
);

  wire not_1_out, not_2_out, or_1_out, or_2_out;

  not not_1 (not_1_out, a);
  not not_2 (not_2_out, b);
  or or_1 (or_1_out, b, c);
  or or_2 (or_2_out, not_1_out, not_2_out, c);
  and and_1 (s, or_1_out, or_2_out);
endmodule

module letraB (
  input  a,
  input  b,
  input  c,
  output out_4
);

  wire functionb_1_s, minimizedb_1_s;

  functionB functionb_1 (.a(a), .b(b), .c(c), .s(functionb_1_s));
  minimizedB minimizedb_1 (.a(a), .b(b), .c(c), .s(minimizedb_1_s));
  xnor xnor_1 (out_4, functionb_1_s, minimizedb_1_s);

  // Notes on the sheet:
  //   Letra B
endmodule

module functionC (
  input  a,
  input  b,
  input  c,
  output s
);

  wire not_1_out, not_2_out, not_3_out, not_4_out, not_5_out, not_6_out, or_1_out, or_2_out, or_3_out,
       or_4_out;

  not not_1 (not_1_out, c);
  not not_2 (not_2_out, b);
  not not_3 (not_3_out, b);
  not not_4 (not_4_out, c);
  not not_5 (not_5_out, a);
  not not_6 (not_6_out, b);
  or or_1 (or_1_out, a, b, not_1_out);
  or or_2 (or_2_out, a, not_2_out, c);
  or or_3 (or_3_out, a, not_3_out, not_4_out);
  or or_4 (or_4_out, not_5_out, not_6_out, c);
  and and_1 (s, or_1_out, or_2_out, or_3_out, or_4_out);
endmodule

module minimizedC (
  input  a,
  input  b,
  input  c,
  output s
);

  wire not_1_out, not_2_out, not_3_out, or_1_out, or_2_out, or_3_out;

  not not_1 (not_1_out, c);
  not not_2 (not_2_out, b);
  not not_3 (not_3_out, b);
  or or_1 (or_1_out, a, not_1_out);
  or or_2 (or_2_out, a, not_2_out);
  or or_3 (or_3_out, not_3_out, c);
  and and_1 (s, or_1_out, or_2_out, or_3_out);
endmodule

module letraC (
  input  a,
  input  b,
  input  c,
  output out_4
);

  wire functionc_1_s, minimizedc_1_s;

  functionC functionc_1 (.a(a), .b(b), .c(c), .s(functionc_1_s));
  minimizedC minimizedc_1 (.a(a), .b(b), .c(c), .s(minimizedc_1_s));
  xnor xnor_1 (out_4, functionc_1_s, minimizedc_1_s);

  // Notes on the sheet:
  //   Letra C
endmodule

module functionD (
  input  a,
  input  b,
  input  c,
  output s
);

  wire not_1_out, not_2_out, not_3_out, not_4_out, not_5_out, or_1_out, or_2_out, or_3_out, or_4_out;

  not not_1 (not_1_out, c);
  not not_2 (not_2_out, a);
  not not_3 (not_3_out, c);
  not not_4 (not_4_out, a);
  not not_5 (not_5_out, b);
  or or_1 (or_1_out, a, b, c);
  or or_2 (or_2_out, a, b, not_1_out);
  or or_3 (or_3_out, not_2_out, b, not_3_out);
  or or_4 (or_4_out, not_4_out, not_5_out, c);
  and and_1 (s, or_1_out, or_2_out, or_3_out, or_4_out);
endmodule

module minimizedD (
  input  a,
  input  b,
  input  c,
  output s
);

  wire not_1_out, not_2_out, not_3_out, or_1_out, or_2_out, or_3_out;

  not not_1 (not_1_out, c);
  not not_2 (not_2_out, a);
  not not_3 (not_3_out, b);
  or or_1 (or_1_out, a, b);
  or or_2 (or_2_out, b, not_1_out);
  or or_3 (or_3_out, not_2_out, not_3_out, c);
  and and_1 (s, or_1_out, or_2_out, or_3_out);
endmodule

module letraD (
  input  a,
  input  b,
  input  c,
  output out_4
);

  wire functiond_1_s, minimizedd_1_s;

  functionD functiond_1 (.a(a), .b(b), .c(c), .s(functiond_1_s));
  minimizedD minimizedd_1 (.a(a), .b(b), .c(c), .s(minimizedd_1_s));
  xnor xnor_1 (out_4, functiond_1_s, minimizedd_1_s);

  // Notes on the sheet:
  //   Letra D
endmodule

module functionE (
  input  a,
  input  b,
  input  c,
  output s
);

  wire not_1_out, not_2_out, not_3_out, not_4_out, not_5_out, or_1_out, or_2_out, or_3_out, or_4_out;

  not not_1 (not_1_out, b);
  not not_2 (not_2_out, a);
  not not_3 (not_3_out, a);
  not not_4 (not_4_out, b);
  not not_5 (not_5_out, c);
  or or_1 (or_1_out, a, b, c);
  or or_2 (or_2_out, a, not_1_out, c);
  or or_3 (or_3_out, not_2_out, b, c);
  or or_4 (or_4_out, not_3_out, not_4_out, not_5_out);
  and and_1 (s, or_1_out, or_2_out, or_3_out, or_4_out);
endmodule

module minimizedE (
  input  a,
  input  b,
  input  c,
  output e
);

  wire not_1_out, not_2_out, not_3_out, or_1_out, or_2_out, or_3_out;

  not not_1 (not_1_out, a);
  not not_2 (not_2_out, b);
  not not_3 (not_3_out, c);
  or or_1 (or_1_out, b, c);
  or or_2 (or_2_out, a, c);
  or or_3 (or_3_out, not_1_out, not_2_out, not_3_out);
  and and_1 (e, or_1_out, or_2_out, or_3_out);
endmodule

module letraE (
  input  a,
  input  b,
  input  c,
  output out_4
);

  wire functione_1_s, minimizede_1_e;

  functionE functione_1 (.a(a), .b(b), .c(c), .s(functione_1_s));
  minimizedE minimizede_1 (.a(a), .b(b), .c(c), .e(minimizede_1_e));
  xnor xnor_1 (out_4, functione_1_s, minimizede_1_e);

  // Notes on the sheet:
  //   Letra E
endmodule
