// Logisim project guia0603.circ as structural Verilog: 15 circuits, main circuit functionA
module functionA (
  input  a,
  input  b,
  input  c,
  input  d,
  output s
);

  wire and_1_out, and_2_out, and_3_out, and_4_out, and_5_out, and_6_out, not_1_out, not_2_out, not_3_out,
       not_4_out, not_5_out, not_6_out, not_7_out, not_8_out, not_9_out, not_10_out, not_11_out, not_12_out,
       not_13_out, not_14_out;

  not not_1 (not_1_out, a);
  not not_2 (not_2_out, b);
  not not_3 (not_3_out, c);
  not not_4 (not_4_out, a);
  not not_5 (not_5_out, b);
  not not_6 (not_6_out, d);
  not not_7 (not_7_out, a);
  not not_8 (not_8_out, d);
  not not_9 (not_9_out, b);
  not not_10 (not_10_out, c);
  not not_11 (not_11_out, d);
  not not_12 (not_12_out, c);
  not not_13 (not_13_out, d);
  not not_14 (not_14_out, d);
  and and_1 (and_1_out, not_1_out, not_2_out, not_3_out, d);
  and and_2 (and_2_out, not_4_out, not_5_out, c, not_6_out);
  and and_3 (and_3_out, not_7_out, b, c, not_8_out);
  and and_4 (and_4_out, a, not_9_out, not_10_out, not_11_out);
  and and_5 (and_5_out, a, b, not_12_out, not_13_out);
  and and_6 (and_6_out, a, b, c, not_14_out);
  or or_1 (s, and_1_out, and_2_out, and_3_out, and_4_out, and_5_out, and_6_out);
endmodule

module minimizedA (
  input  a,
  input  b,
  input  c,
  input  d,
  output s
);

  wire and_1_out, and_2_out, and_3_out, and_4_out, and_5_out, not_1_out, not_2_out, not_3_out, not_4_out,
       not_5_out, not_6_out, not_7_out, not_8_out, not_9_out;

  not not_1 (not_1_out, a);
  not not_2 (not_2_out, b);
  not not_3 (not_3_out, c);
  not not_4 (not_4_out, a);
  not not_5 (not_5_out, d);
  not not_6 (not_6_out, d);
  not not_7 (not_7_out, d);
  not not_8 (not_8_out, c);
  not not_9 (not_9_out, d);
  and and_1 (and_1_out, not_1_out, not_2_out, not_3_out, d);
  and and_2 (and_2_out, not_4_out, c, not_5_out);
  and and_3 (and_3_out, b, c, not_6_out);
  and and_4 (and_4_out, a, b, not_7_out);
  and and_5 (and_5_out, a, not_8_out, not_9_out);
  or or_1 (s, and_1_out, and_2_out, and_3_out, and_4_out, and_5_out);
endmodule

module letraA (
  input  a,
  input  b,
  input  c,
  input  d,
  output out_5
);

  wire functiona_1_s, minimizeda_1_s;

  minimizedA minimizeda_1 (.a(a), .b(b), .c(c), .d(d), .s(minimizeda_1_s));
  functionA functiona_1 (.a(a), .b(b), .c(c), .d(d), .s(functiona_1_s));
  xnor xnor_1 (out_5, functiona_1_s, minimizeda_1_s);

  // Notes on the sheet:
  //   Letra A
endmodule

module functionB (
  input  a,
  input  b,
  input  c,
  input  d,
  output s
);

  wire and_1_out, and_2_out, and_3_out, and_4_out, and_5_out, and_6_out, and_7_out, not_1_out, not_2_out,
       not_3_out, not_4_out, not_5_out, not_6_out, not_7_out, not_8_out, not_9_out, not_10_out, not_11_out,
       not_12_out, not_13_out, not_14_out, not_15_out;

  not not_1 (not_1_out, a);
  not not_2 (not_2_out, b);
  not not_3 (not_3_out, c);
  not not_4 (not_4_out, d);
  not not_5 (not_5_out, a);
  not not_6 (not_6_out, b);
  not not_7 (not_7_out, c);
  not not_8 (not_8_out, a);
  not not_9 (not_9_out, b);
  not not_10 (not_10_out, a);
  not not_11 (not_11_out, b);
  not not_12 (not_12_out, c);
  not not_13 (not_13_out, d);
  not not_14 (not_14_out, c);
  not not_15 (not_15_out, d);
  and and_1 (and_1_out, not_1_out, not_2_out, not_3_out, not_4_out);
  and and_2 (and_2_out, not_5_out, not_6_out, not_7_out, d);
  and and_3 (and_3_out, not_8_out, not_9_out, c, d);
  and and_4 (and_4_out, not_10_out, b, c, d);
  and and_5 (and_5_out, a, not_11_out, not_12_out, not_13_out);
  and and_6 (and_6_out, a, b, not_14_out, not_15_out);
  and and_7 (and_7_out, a, b, c, d);
  or or_1 (s, and_1_out, and_2_out, and_3_out, and_4_out, and_5_out, and_6_out, and_7_out);
endmodule

module minimizedB (
  input  a,
  input  b,
  input  c,
  input  d,
  output s
);

  wire and_1_out, and_2_out, and_3_out, and_4_out, and_5_out, not_1_out, not_2_out, not_3_out, not_4_out,
       not_5_out, not_6_out, not_7_out, not_8_out;

  not not_1 (not_1_out, a);
  and and_1 (and_1_out, not_1_out, not_2_out, not_3_out);
  not not_2 (not_2_out, b);
  not not_3 (not_3_out, c);
  not not_4 (not_4_out, a);
  not not_5 (not_5_out, b);
  and and_2 (and_2_out, not_4_out, not_5_out, d);
  not not_6 (not_6_out, a);
  and and_3 (and_3_out, not_6_out, c, d);
  and and_4 (and_4_out, b, c, d);
  and and_5 (and_5_out, a, not_7_out, not_8_out);
  not not_7 (not_7_out, c);
  not not_8 (not_8_out, d);
  or or_1 (s, and_1_out, and_2_out, and_3_out, and_4_out, and_5_out);
endmodule

module letraB (
  input  a,
  input  b,
  input  c,
  input  d,
  output out_5
);

  wire functionb_1_s, minimizedb_1_s;

  functionB functionb_1 (.a(a), .b(b), .c(c), .d(d), .s(functionb_1_s));
  minimizedB minimizedb_1 (.a(a), .b(b), .c(c), .d(d), .s(minimizedb_1_s));
  xnor xnor_1 (out_5, functionb_1_s, minimizedb_1_s);

  // Notes on the sheet:
  //   Letra B
endmodule

module functionC (
  input  a,
  input  b,
  input  c,
  input  d,
  output s
);

  wire and_1_out, and_2_out, and_3_out, and_4_out, and_5_out, and_6_out, and_7_out, and_8_out, not_1_out,
       not_2_out, not_3_out, not_4_out, not_5_out, not_6_out, not_7_out, not_8_out, not_9_out, not_10_out,
       not_11_out, not_12_out, not_13_out, not_14_out, not_15_out;

  not not_1 (not_1_out, a);
  not not_2 (not_2_out, b);
  not not_3 (not_3_out, c);
  not not_4 (not_4_out, d);
  not not_5 (not_5_out, a);
  not not_6 (not_6_out, b);
  not not_7 (not_7_out, c);
  not not_8 (not_8_out, a);
  not not_9 (not_9_out, b);
  not not_10 (not_10_out, d);
  not not_11 (not_11_out, a);
  not not_12 (not_12_out, b);
  not not_13 (not_13_out, d);
  not not_14 (not_14_out, b);
  not not_15 (not_15_out, d);
  and and_1 (and_1_out, not_1_out, not_2_out, not_3_out, not_4_out);
  and and_2 (and_2_out, not_5_out, not_6_out, not_7_out, d);
  and and_3 (and_3_out, not_8_out, not_9_out, c, not_10_out);
  and and_4 (and_4_out, not_11_out, b, c, d);
  and and_5 (and_5_out, a, not_12_out, c, not_13_out);
  and and_6 (and_6_out, a, not_14_out, c, d);
  and and_7 (and_7_out, a, b, c, not_15_out);
  and and_8 (and_8_out, a, b, c, d);
  or or_1 (s, and_1_out, and_2_out, and_3_out, and_4_out, and_5_out, and_6_out, and_7_out, and_8_out);
endmodule

module minimizedC (
  input  a,
  input  b,
  input  c,
  input  d,
  output s
);

  wire and_1_out, and_2_out, and_3_out, and_4_out, not_1_out, not_2_out, not_3_out, not_4_out, not_5_out,
       not_6_out;

  not not_1 (not_1_out, a);
  not not_2 (not_2_out, b);
  and and_1 (and_1_out, not_1_out, not_2_out, not_3_out);
  not not_3 (not_3_out, d);
  not not_4 (not_4_out, a);
  and and_2 (and_2_out, not_4_out, not_5_out, not_6_out);
  not not_5 (not_5_out, b);
  not not_6 (not_6_out, c);
  and and_3 (and_3_out, b, c, d);
  and and_4 (and_4_out, a, c);
  or or_1 (s, and_1_out, and_2_out, and_3_out, and_4_out);
endmodule

module letraC (
  input  a,
  input  b,
  input  c,
  input  d,
  output out_5
);

  wire functionc_1_s, minimizedc_1_s;

  functionC functionc_1 (.a(a), .b(b), .c(c), .d(d), .s(functionc_1_s));
  minimizedC minimizedc_1 (.a(a), .b(b), .c(c), .d(d), .s(minimizedc_1_s));
  xnor xnor_1 (out_5, functionc_1_s, minimizedc_1_s);

  // Notes on the sheet:
  //   Letra C
endmodule

module functionD (
  input  a,
  input  b,
  input  c,
  input  d,
  output s
);

  wire and_1_out, and_2_out, and_3_out, and_4_out, and_5_out, and_6_out, and_7_out, not_1_out, not_2_out,
       not_3_out, not_4_out, not_5_out, not_6_out, not_7_out, not_8_out, not_9_out, not_10_out, not_11_out,
       not_12_out, not_13_out, not_14_out;

  not not_1 (not_1_out, a);
  not not_2 (not_2_out, b);
  not not_3 (not_3_out, d);
  not not_4 (not_4_out, a);
  not not_5 (not_5_out, c);
  not not_6 (not_6_out, d);
  not not_7 (not_7_out, a);
  not not_8 (not_8_out, c);
  not not_9 (not_9_out, a);
  not not_10 (not_10_out, d);
  not not_11 (not_11_out, b);
  not not_12 (not_12_out, d);
  not not_13 (not_13_out, c);
  not not_14 (not_14_out, d);
  and and_1 (and_1_out, not_1_out, not_2_out, c, not_3_out);
  and and_2 (and_2_out, not_4_out, b, not_5_out, not_6_out);
  and and_3 (and_3_out, not_7_out, b, not_8_out, d);
  and and_4 (and_4_out, not_9_out, b, c, not_10_out);
  and and_5 (and_5_out, a, not_11_out, c, not_12_out);
  and and_6 (and_6_out, a, b, not_13_out, d);
  and and_7 (and_7_out, a, b, c, not_14_out);
  or or_1 (s, and_1_out, and_2_out, and_3_out, and_4_out, and_5_out, and_6_out, and_7_out);
endmodule

module minimizedD (
  input  a,
  input  b,
  input  c,
  input  d,
  output s
);

  wire and_1_out, and_2_out, and_3_out, and_4_out, and_5_out, not_1_out, not_2_out, not_3_out, not_4_out,
       not_5_out, not_6_out, not_7_out;

  not not_1 (not_1_out, a);
  and and_1 (and_1_out, not_1_out, c, not_2_out);
  not not_2 (not_2_out, d);
  and and_2 (and_2_out, b, c, not_3_out);
  not not_3 (not_3_out, d);
  and and_3 (and_3_out, a, c, not_4_out);
  not not_4 (not_4_out, d);
  not not_5 (not_5_out, a);
  and and_4 (and_4_out, not_5_out, b, not_6_out);
  not not_6 (not_6_out, c);
  and and_5 (and_5_out, b, not_7_out, d);
  not not_7 (not_7_out, c);
  or or_1 (s, and_1_out, and_2_out, and_3_out, and_4_out, and_5_out);
endmodule

module letraD (
  input  a,
  input  b,
  input  c,
  input  d,
  output out_5
);

  wire functiond_1_s, minimizedd_1_s;

  functionD functiond_1 (.a(a), .b(b), .c(c), .d(d), .s(functiond_1_s));
  minimizedD minimizedd_1 (.a(a), .b(b), .c(c), .d(d), .s(minimizedd_1_s));
  xnor xnor_1 (out_5, functiond_1_s, minimizedd_1_s);

  // Notes on the sheet:
  //   Letra D
endmodule

module functionE (
  input  a,
  input  b,
  input  c,
  input  d,
  output s
);

  wire and_1_out, and_2_out, and_3_out, and_4_out, and_5_out, and_6_out, and_7_out, and_8_out, not_1_out,
       not_2_out, not_3_out, not_4_out, not_5_out, not_6_out, not_7_out, not_8_out, not_9_out, not_10_out,
       not_11_out, not_12_out, not_13_out, not_14_out, not_15_out, not_16_out, not_17_out, not_18_out;

  not not_1 (not_1_out, a);
  not not_2 (not_2_out, b);
  not not_3 (not_3_out, c);
  not not_4 (not_4_out, d);
  not not_5 (not_5_out, a);
  not not_6 (not_6_out, b);
  not not_7 (not_7_out, c);
  not not_8 (not_8_out, a);
  not not_9 (not_9_out, b);
  not not_10 (not_10_out, a);
  not not_11 (not_11_out, c);
  not not_12 (not_12_out, b);
  not not_13 (not_13_out, c);
  not not_14 (not_14_out, d);
  not not_15 (not_15_out, b);
  not not_16 (not_16_out, c);
  not not_17 (not_17_out, b);
  not not_18 (not_18_out, c);
  and and_1 (and_1_out, not_1_out, not_2_out, not_3_out, not_4_out);
  and and_2 (and_2_out, not_5_out, not_6_out, not_7_out, d);
  and and_3 (and_3_out, not_8_out, not_9_out, c, d);
  and and_4 (and_4_out, not_10_out, b, not_11_out, d);
  and and_5 (and_5_out, a, not_12_out, not_13_out, not_14_out);
  and and_6 (and_6_out, a, not_15_out, not_16_out, d);
  and and_7 (and_7_out, a, not_17_out, c, d);
  and and_8 (and_8_out, a, b, not_18_out, d);
  or or_1 (s, and_1_out, and_2_out, and_3_out, and_4_out, and_5_out, and_6_out, and_7_out, and_8_out);
endmodule

module minimizedE (
  input  a,
  input  b,
  input  c,
  input  d,
  output s
);

  wire and_1_out, and_2_out, and_3_out, not_1_out, not_2_out, not_3_out, not_4_out;

  not not_1 (not_1_out, c);
  and and_1 (and_1_out, not_1_out, d);
  not not_2 (not_2_out, b);
  and and_2 (and_2_out, not_2_out, d);
  not not_3 (not_3_out, b);
  and and_3 (and_3_out, not_3_out, not_4_out);
  not not_4 (not_4_out, c);
  or or_1 (s, and_1_out, and_2_out, and_3_out);
endmodule

module letraE (
  input  a,
  input  b,
  input  c,
  input  d,
  output out_5
);

  wire functione_1_s, minimizede_1_s;

  functionE functione_1 (.a(a), .b(b), .c(c), .d(d), .s(functione_1_s));
  minimizedE minimizede_1 (.a(a), .b(b), .c(c), .d(d), .s(minimizede_1_s));
  xnor xnor_1 (out_5, functione_1_s, minimizede_1_s);

  // Notes on the sheet:
  //   Letra E
endmodule
