// Logisim project guia0604.circ as structural Verilog: 15 circuits, main circuit letraA
module functionA (
  input  a,
  input  b,
  input  c,
  input  d,
  output s
);

  wire not_1_out, not_2_out, not_3_out, not_4_out, not_5_out, not_6_out, not_7_out, not_8_out, not_9_out,
       or_1_out, or_2_out, or_3_out, or_4_out;

  not not_1 (not_1_out, c);
  not not_2 (not_2_out, b);
  not not_3 (not_3_out, d);
  not not_4 (not_4_out, b);
  not not_5 (not_5_out, c);
  not not_6 (not_6_out, d);
  not not_7 (not_7_out, a);
  not not_8 (not_8_out, b);
  not not_9 (not_9_out, d);
  or or_1 (or_1_out, a, b, not_1_out, d);
  or or_2 (or_2_out, a, not_2_out, c, not_3_out);
  or or_3 (or_3_out, a, not_4_out, not_5_out, not_6_out);
  or or_4 (or_4_out, not_7_out, not_8_out, c, not_9_out);
  and and_1 (s, or_1_out, or_2_out, or_3_out, or_4_out);
endmodule

module minimizedA (
  input  a,
  input  b,
  input  c,
  input  d,
  output s
);

  wire not_1_out, not_2_out, not_3_out, not_4_out, not_5_out, or_1_out, or_2_out, or_3_out;

  not not_1 (not_1_out, c);
  not not_2 (not_2_out, b);
  not not_3 (not_3_out, d);
  not not_4 (not_4_out, b);
  not not_5 (not_5_out, d);
  or or_1 (or_1_out, a, b, not_1_out, d);
  and and_1 (s, or_1_out, or_2_out, or_3_out);
  or or_2 (or_2_out, a, not_2_out, not_3_out);
  or or_3 (or_3_out, not_4_out, c, not_5_out);
endmodule

module letraA (
  input  a,
  input  b,
  input  c,
  input  d,
  output out_5
);

  wire functiona_1_s, minimizeda_1_s;

  functionA functiona_1 (.a(a), .b(b), .c(c), .d(d), .s(functiona_1_s));
  minimizedA minimizeda_1 (.a(a), .b(b), .c(c), .d(d), .s(minimizeda_1_s));
  xnor xnor_1 (out_5, functiona_1_s, minimizeda_1_s);

  // Notes on the sheet:
  //   Letra A
endmodule

module functionB (
  input  a,
  input  b,
  input  c,
  input  d,
  output s
);

  wire not_1_out, not_2_out, not_3_out, not_4_out, not_5_out, not_6_out, not_7_out, not_8_out, not_9_out,
       not_10_out, not_11_out, or_1_out, or_2_out, or_3_out, or_4_out, or_5_out;

  not not_1 (not_1_out, b);
  not not_2 (not_2_out, b);
  not not_3 (not_3_out, c);
  not not_4 (not_4_out, a);
  not not_5 (not_5_out, d);
  not not_6 (not_6_out, a);
  not not_7 (not_7_out, c);
  not not_8 (not_8_out, d);
  not not_9 (not_9_out, a);
  not not_10 (not_10_out, b);
  not not_11 (not_11_out, c);
  or or_1 (or_1_out, a, not_1_out, c, d);
  or or_2 (or_2_out, a, not_2_out, not_3_out, d);
  or or_3 (or_3_out, not_4_out, b, c, not_5_out);
  or or_4 (or_4_out, not_6_out, b, not_7_out, not_8_out);
  or or_5 (or_5_out, not_9_out, not_10_out, not_11_out, d);
  and and_1 (s, or_1_out, or_2_out, or_3_out, or_4_out, or_5_out);
endmodule

module minimizedB (
  input  a,
  input  b,
  input  c,
  input  d,
  output s
);

  wire not_1_out, not_2_out, not_3_out, not_4_out, not_5_out, or_1_out, or_2_out, or_3_out;

  or or_1 (or_1_out, a, not_1_out, d);
  not not_1 (not_1_out, b);
  not not_2 (not_2_out, b);
  or or_2 (or_2_out, not_2_out, not_3_out, d);
  not not_3 (not_3_out, c);
  not not_4 (not_4_out, a);
  or or_3 (or_3_out, not_4_out, b, not_5_out);
  not not_5 (not_5_out, d);
  and and_1 (s, or_1_out, or_2_out, or_3_out);
endmodule

module letraB (
  input  a,
  input  b,
  input  c,
  input  d,
  output out_5
);

  wire functionb_1_s, minimizedb_1_s;

  functionB functionb_1 (.a(a), .b(b), .c(c), .d(d), .s(functionb_1_s));
  minimizedB minimizedb_1 (.a(a), .b(b), .c(c), .d(d), .s(minimizedb_1_s));
  xnor xnor_1 (out_5, functionb_1_s, minimizedb_1_s);

  // Notes on the sheet:
  //   Letra B
endmodule

module functionC (
  input  a,
  input  b,
  input  c,
  input  d,
  output s
);

  wire not_1_out, not_2_out, not_3_out, not_4_out, not_5_out, not_6_out, not_7_out, not_8_out, not_9_out,
       or_1_out, or_2_out, or_3_out, or_4_out, or_5_out;

  not not_1 (not_1_out, b);
  not not_2 (not_2_out, b);
  not not_3 (not_3_out, c);
  not not_4 (not_4_out, d);
  not not_5 (not_5_out, a);
  not not_6 (not_6_out, a);
  not not_7 (not_7_out, c);
  not not_8 (not_8_out, a);
  not not_9 (not_9_out, b);
  or or_1 (or_1_out, a, not_1_out, c, d);
  or or_2 (or_2_out, a, not_2_out, not_3_out, not_4_out);
  or or_3 (or_3_out, not_5_out, b, c, d);
  or or_4 (or_4_out, not_6_out, b, not_7_out, d);
  or or_5 (or_5_out, not_8_out, not_9_out, c, d);
  and and_1 (s, or_1_out, or_2_out, or_3_out, or_4_out, or_5_out);
endmodule

module minimizedC (
  input  a,
  input  b,
  input  c,
  input  d,
  output s
);

  wire not_1_out, not_2_out, not_3_out, not_4_out, not_5_out, or_1_out, or_2_out, or_3_out;

  not not_1 (not_1_out, b);
  not not_2 (not_2_out, c);
  not not_3 (not_3_out, d);
  not not_4 (not_4_out, b);
  not not_5 (not_5_out, a);
  or or_1 (or_1_out, a, not_1_out, not_2_out, not_3_out);
  and and_1 (s, or_1_out, or_2_out, or_3_out);
  or or_2 (or_2_out, not_4_out, c, d);
  or or_3 (or_3_out, not_5_out, b, d);
endmodule

module letraC (
  input  a,
  input  b,
  input  c,
  input  d,
  output out_5
);

  wire functionc_1_s, minimizedc_1_s;

  functionC functionc_1 (.a(a), .b(b), .c(c), .d(d), .s(functionc_1_s));
  minimizedC minimizedc_1 (.a(a), .b(b), .c(c), .d(d), .s(minimizedc_1_s));
  xnor xnor_1 (out_5, functionc_1_s, minimizedc_1_s);

  // Notes on the sheet:
  //   Letra C
endmodule

module functionD (
  input  a,
  input  b,
  input  c,
  input  d,
  output s
);

  wire not_1_out, not_2_out, not_3_out, not_4_out, not_5_out, not_6_out, not_7_out, not_8_out, not_9_out,
       not_10_out, not_11_out, not_12_out, not_13_out, not_14_out, not_15_out, or_1_out, or_2_out, or_3_out,
       or_4_out, or_5_out, or_6_out;

  not not_1 (not_1_out, d);
  not not_2 (not_2_out, b);
  not not_3 (not_3_out, d);
  not not_4 (not_4_out, a);
  not not_5 (not_5_out, d);
  not not_6 (not_6_out, a);
  not not_7 (not_7_out, c);
  not not_8 (not_8_out, d);
  not not_9 (not_9_out, a);
  not not_10 (not_10_out, b);
  not not_11 (not_11_out, d);
  not not_12 (not_12_out, a);
  not not_13 (not_13_out, b);
  not not_14 (not_14_out, c);
  not not_15 (not_15_out, d);
  or or_1 (or_1_out, a, b, c, not_1_out);
  or or_2 (or_2_out, a, not_2_out, c, not_3_out);
  or or_3 (or_3_out, not_4_out, b, c, not_5_out);
  or or_4 (or_4_out, not_6_out, b, not_7_out, not_8_out);
  or or_5 (or_5_out, not_9_out, not_10_out, c, not_11_out);
  or or_6 (or_6_out, not_12_out, not_13_out, not_14_out, not_15_out);
  and and_1 (s, or_1_out, or_2_out, or_3_out, or_4_out, or_5_out, or_6_out);
endmodule

module minimizedD (
  input  a,
  input  b,
  input  c,
  input  d,
  output s
);

  wire not_1_out, not_2_out, not_3_out, or_1_out, or_2_out;

  or or_1 (or_1_out, c, not_1_out);
  not not_1 (not_1_out, d);
  not not_2 (not_2_out, a);
  or or_2 (or_2_out, not_2_out, not_3_out);
  not not_3 (not_3_out, d);
  and and_1 (s, or_1_out, or_2_out);
endmodule

module letraD (
  input  a,
  input  b,
  input  c,
  input  d,
  output out_5
);

  wire functiond_1_s, minimizedd_1_s;

  functionD functiond_1 (.a(a), .b(b), .c(c), .d(d), .s(functiond_1_s));
  minimizedD minimizedd_1 (.a(a), .b(b), .c(c), .d(d), .s(minimizedd_1_s));
  xnor xnor_1 (out_5, functiond_1_s, minimizedd_1_s);

  // Notes on the sheet:
  //   Letra D
endmodule

module functionE (
  input  a,
  input  b,
  input  c,
  input  d,
  output s
);

  wire not_1_out, not_2_out, not_3_out, not_4_out, not_5_out, not_6_out, not_7_out, not_8_out, not_9_out,
       not_10_out, not_11_out, not_12_out, not_13_out, not_14_out, not_15_out, not_16_out, not_17_out,
       or_1_out, or_2_out, or_3_out, or_4_out, or_5_out, or_6_out, or_7_out;

  not not_1 (not_1_out, c);
  not not_2 (not_2_out, c);
  not not_3 (not_3_out, d);
  not not_4 (not_4_out, b);
  not not_5 (not_5_out, c);
  not not_6 (not_6_out, b);
  not not_7 (not_7_out, c);
  not not_8 (not_8_out, d);
  not not_9 (not_9_out, a);
  not not_10 (not_10_out, c);
  not not_11 (not_11_out, d);
  not not_12 (not_12_out, a);
  not not_13 (not_13_out, b);
  not not_14 (not_14_out, d);
  not not_15 (not_15_out, a);
  not not_16 (not_16_out, b);
  not not_17 (not_17_out, c);
  or or_1 (or_1_out, a, b, not_1_out, d);
  or or_2 (or_2_out, a, b, not_2_out, not_3_out);
  or or_3 (or_3_out, a, not_4_out, not_5_out, d);
  or or_4 (or_4_out, a, not_6_out, not_7_out, not_8_out);
  or or_5 (or_5_out, not_9_out, b, not_10_out, not_11_out);
  or or_6 (or_6_out, not_12_out, not_13_out, c, not_14_out);
  or or_7 (or_7_out, not_15_out, not_16_out, not_17_out, d);
  and and_1 (s, or_1_out, or_2_out, or_3_out, or_4_out, or_5_out, or_6_out, or_7_out);
endmodule

module minimizedE (
  input  a,
  input  b,
  input  c,
  input  d,
  output s
);

  wire not_1_out, not_2_out, not_3_out, not_4_out, not_5_out, not_6_out, not_7_out, not_8_out, or_1_out,
       or_2_out, or_3_out, or_4_out;

  not not_1 (not_1_out, a);
  not not_2 (not_2_out, b);
  not not_3 (not_3_out, d);
  not not_4 (not_4_out, c);
  not not_5 (not_5_out, d);
  not not_6 (not_6_out, c);
  not not_7 (not_7_out, b);
  not not_8 (not_8_out, c);
  or or_1 (or_1_out, not_1_out, not_2_out, c, not_3_out);
  or or_2 (or_2_out, b, not_4_out, not_5_out);
  or or_3 (or_3_out, a, not_6_out);
  or or_4 (or_4_out, not_7_out, not_8_out, d);
  and and_1 (s, or_1_out, or_2_out, or_3_out, or_4_out);
endmodule

module letraE (
  input  a,
  input  b,
  input  c,
  input  d,
  output out_5
);

  wire functione_1_s, minimizede_1_s;

  functionE functione_1 (.a(a), .b(b), .c(c), .d(d), .s(functione_1_s));
  minimizedE minimizede_1 (.a(a), .b(b), .c(c), .d(d), .s(minimizede_1_s));
  xnor xnor_1 (out_5, functione_1_s, minimizede_1_s);

  // Notes on the sheet:
  //   Letra E
endmodule
