// Logisim project guia0605.circ as structural Verilog: 3 circuits, main circuit main
module main (
  input  a,
  input  b,
  input  c,
  output out_4
);

  wire function_1_s, minimized_1_s;

  \function  function_1 (.a(a), .b(b), .c(c), .s(function_1_s));
  minimized minimized_1 (.a(a), .b(b), .c(c), .s(minimized_1_s));
  xnor xnor_1 (out_4, function_1_s, minimized_1_s);
endmodule

module \function  (
  input  a,
  input  b,
  input  c,
  output s
);

  wire and_1_out, and_2_out, and_3_out, and_4_out, not_1_out, not_2_out, not_3_out, not_4_out, not_5_out,
       not_6_out, or_1_out;

  not not_1 (not_1_out, a);
  not not_2 (not_2_out, b);
  not not_3 (not_3_out, and_1_out);
  and and_1 (and_1_out, not_1_out, not_2_out);
  not not_4 (not_4_out, and_2_out);
  and and_2 (and_2_out, a, b);
  and and_3 (and_3_out, b, c);
  not not_5 (not_5_out, a);
  and and_4 (and_4_out, not_3_out, not_4_out);
  or or_1 (or_1_out, and_3_out, not_5_out);
  not not_6 (not_6_out, or_1_out);
  or or_2 (s, and_4_out, not_6_out);
endmodule

module minimized (
  input  a,
  input  b,
  input  c,
  output s
);

  wire and_1_out, and_2_out, not_1_out, not_2_out;

  not not_1 (not_1_out, b);
  not not_2 (not_2_out, c);
  and and_1 (and_1_out, a, not_1_out);
  and and_2 (and_2_out, a, not_2_out);
  or or_1 (s, and_1_out, and_2_out);
endmodule
