// Logisim project guia0606.circ as structural Verilog: 3 circuits, main circuit main
module main (
  input  a,
  input  b,
  input  c,
  input  d,
  output out_5
);

  wire function_1_s, minimized_1_s;

  \function  function_1 (.X(a), .Y(b), .W(c), .Z(d), .s(function_1_s));
  minimized minimized_1 (.X(a), .Y(b), .W(c), .Z(d), .s(minimized_1_s));
  xnor xnor_1 (out_5, function_1_s, minimized_1_s);
endmodule

module \function  (
  input  X,
  input  Y,
  input  W,
  input  Z,
  output s
);

  wire and_1_out, and_2_out, nand_1_out, nor_1_out, nor_2_out, not_1_out, not_2_out, not_3_out, not_4_out;

  not not_1 (not_1_out, X);
  not not_2 (not_2_out, Y);
  not not_3 (not_3_out, W);
  and and_1 (and_1_out, Y, W, Z);
  not not_4 (not_4_out, X);
  nor nor_1 (nor_1_out, not_1_out, not_2_out, W);
  and and_2 (and_2_out, nor_1_out, nand_1_out);
  nand nand_1 (nand_1_out, X, Y, not_3_out);
  nor nor_2 (nor_2_out, and_1_out, not_4_out);
  or or_1 (s, and_2_out, nor_2_out);
endmodule

module minimized (
  input  X,
  input  Y,
  input  W,
  input  Z,
  output s
);

  wire not_1_out, not_2_out, not_3_out, or_1_out;

  not not_1 (not_1_out, Y);
  or or_1 (or_1_out, not_1_out, not_2_out, not_3_out);
  not not_2 (not_2_out, W);
  not not_3 (not_3_out, Z);
  and and_1 (s, X, or_1_out);
endmodule
