// Logisim project guia0607.circ as structural Verilog: 3 circuits, main circuit main
module main (
  input  a,
  input  b,
  input  c,
  output out_4
);

  wire function_1_s, minimized_1_s;

  \function  function_1 (.x(a), .y(b), .z(c), .s(function_1_s));
  minimized minimized_1 (.x(a), .y(b), .z(c), .s(minimized_1_s));
  xnor xnor_1 (out_4, function_1_s, minimized_1_s);
endmodule

module \function  (
  input  x,
  input  y,
  input  z,
  output s
);

  wire not_1_out, not_2_out, not_3_out, not_4_out, or_1_out, or_2_out, or_3_out;

  not not_1 (not_1_out, x);
  not not_2 (not_2_out, y);
  not not_3 (not_3_out, x);
  not not_4 (not_4_out, y);
  or or_1 (or_1_out, x, y, z);
  or or_2 (or_2_out, not_1_out, not_2_out, z);
  or or_3 (or_3_out, not_3_out, not_4_out, z);
  and and_1 (s, or_1_out, or_2_out, or_3_out);
endmodule

module minimized (
  input  x,
  input  y,
  input  z,
  output s
);

  wire not_1_out, not_2_out, or_1_out, or_2_out;

  not not_1 (not_1_out, x);
  not not_2 (not_2_out, y);
  or or_1 (or_1_out, x, y, z);
  or or_2 (or_2_out, not_1_out, not_2_out, z);
  and and_1 (s, or_1_out, or_2_out);
endmodule
