// Logisim project guia0608.circ as structural Verilog: 3 circuits, main circuit main
module main (
  input  a,
  input  b,
  input  c,
  input  d,
  output out_5
);

  wire function_1_s, minimized_1_s;

  \function  function_1 (.x(a), .y(b), .w(c), .z(d), .s(function_1_s));
  minimized minimized_1 (.a(a), .b(b), .c(c), .d(d), .s(minimized_1_s));
  xnor xnor_1 (out_5, function_1_s, minimized_1_s);
endmodule

module \function  (
  input  x,
  input  y,
  input  w,
  input  z,
  output s
);

  wire and_1_out, and_2_out, and_3_out, and_4_out, not_1_out, not_2_out, not_3_out, not_4_out, not_5_out,
       not_6_out, not_7_out, not_8_out;

  not not_1 (not_1_out, x);
  not not_2 (not_2_out, y);
  not not_3 (not_3_out, z);
  not not_4 (not_4_out, y);
  not not_5 (not_5_out, w);
  not not_6 (not_6_out, z);
  not not_7 (not_7_out, w);
  not not_8 (not_8_out, z);
  and and_1 (and_1_out, not_1_out, not_2_out, w, not_3_out);
  and and_2 (and_2_out, x, not_4_out, not_5_out, not_6_out);
  and and_3 (and_3_out, x, y, not_7_out, z);
  and and_4 (and_4_out, x, y, w, not_8_out);
  or or_1 (s, and_1_out, and_2_out, and_3_out, and_4_out);
endmodule

module minimized (
  input  a,
  input  b,
  input  c,
  input  d,
  output s
);

  wire and_1_out, and_2_out, and_3_out, and_4_out, not_1_out, not_2_out, not_3_out, not_4_out, not_5_out,
       not_6_out, not_7_out, not_8_out;

  not not_1 (not_1_out, b);
  not not_2 (not_2_out, c);
  not not_3 (not_3_out, d);
  not not_4 (not_4_out, c);
  not not_5 (not_5_out, d);
  not not_6 (not_6_out, a);
  not not_7 (not_7_out, b);
  not not_8 (not_8_out, d);
  and and_1 (and_1_out, a, not_1_out, not_2_out, not_3_out);
  and and_2 (and_2_out, a, b, not_4_out, d);
  and and_3 (and_3_out, a, b, c, not_5_out);
  and and_4 (and_4_out, not_6_out, not_7_out, c, not_8_out);
  or or_1 (s, and_1_out, and_2_out, and_3_out, and_4_out);
endmodule
