// Logisim project guia0703.circ as structural Verilog: 1 circuit, main circuit main
module main (
  input  a,
  input  b,
  input  d,
  input  c,
  output out_5
);

  wire and_1_out, multiplexer_1_out, multiplexer_2_out, nand_1_out, nor_1_out, or_1_out;

  or or_1 (or_1_out, a, b);
  nor nor_1 (nor_1_out, a, b);
  and and_1 (and_1_out, a, b);
  nand nand_1 (nand_1_out, a, b);
  Multiplexer #(.enable("false")) multiplexer_1 (.in0(or_1_out), .in1(nor_1_out), .out(multiplexer_1_out), .sel(c));
  Multiplexer #(.enable("false")) multiplexer_2 (.in0(and_1_out), .in1(nand_1_out), .out(multiplexer_2_out), .sel(c));
  Multiplexer #(.enable("false")) multiplexer_3 (
    .in0(multiplexer_1_out), .in1(multiplexer_2_out), .out(out_5), .sel(d));
endmodule
