// Logisim project guia0704.circ as structural Verilog: 1 circuit, main circuit main
module main (
  input  a,
  input  b,
  input  [1:0] d,
  output out_4
);

  wire nor_1_out, or_1_out, xnor_1_out, xor_1_out;

  or or_1 (or_1_out, a, b);
  nor nor_1 (nor_1_out, a, b);
  xor xor_1 (xor_1_out, a, b);
  xnor xnor_1 (xnor_1_out, a, b);
  Multiplexer #(.select(2), .enable("false")) multiplexer_1 (
    .in0(xnor_1_out), .in1(xor_1_out), .in2(or_1_out), .in3(nor_1_out), .out(out_4), .sel(d));
endmodule
