// Logisim project guia0705.circ as structural Verilog: 1 circuit, main circuit main
module main (
  input  [2:0] d,
  input  a,
  input  b,
  output out_4
);

  wire and_1_out, nand_1_out, nor_1_out, not_1_out, not_2_out, or_1_out, xnor_1_out, xor_1_out;

  and and_1 (and_1_out, a, b);
  nand nand_1 (nand_1_out, a, b);
  or or_1 (or_1_out, a, b);
  nor nor_1 (nor_1_out, a, b);
  xor xor_1 (xor_1_out, a, b);
  xnor xnor_1 (xnor_1_out, a, b);
  not not_1 (not_1_out, a);
  not not_2 (not_2_out, b);
  Multiplexer #(.select(3), .enable("false")) multiplexer_1 (
    .in0(not_1_out), .in1(and_1_out), .in2(nand_1_out), .in3(or_1_out), .in4(nor_1_out), .in5(xor_1_out),
    .in6(xnor_1_out), .in7(not_2_out), .out(out_4), .sel(d));
endmodule
