// Logisim project guia0706.circ as structural Verilog: 1 circuit, main circuit main
module main (
  input  [3:0] in_1,
  input  [3:0] in_2,
  input  in_3,
  output [3:0] out_4
);

  wire [3:0] xnor_1_out, xor_1_out;

  assign xor_1_out = in_1 ^ in_2;  // XOR_Gate xor_1, 4 bits wide
  assign xnor_1_out = ~(in_1 ^ in_2);  // XNOR_Gate xnor_1, 4 bits wide
  Multiplexer #(.width(4), .enable("false")) multiplexer_1 (.in0(xor_1_out), .in1(xnor_1_out), .out(out_4), .sel(in_3));
endmodule
