// Logisim project guia0801.circ as structural Verilog: 3 circuits, main circuit main
module main (
  input  in_1,
  input  in_2,
  input  in_3,
  input  in_4,
  input  in_5,
  input  in_6,
  input  in_7,
  input  in_8,
  input  in_9,
  input  in_10,
  output [5:0] out_11
);

  wire fa_2_carry_out, fa_3_carry_out, fa_4_carry_out, fa_5_carry_out;

  fa fa_1 (.carry_out(out_11[5]), .answer(out_11[4]), .in_1(in_1), .in_2(in_6), .carry_in(fa_2_carry_out));
  fa fa_2 (.carry_out(fa_2_carry_out), .answer(out_11[3]), .in_1(in_2), .in_2(in_7), .carry_in(fa_3_carry_out));
  fa fa_3 (.carry_out(fa_3_carry_out), .answer(out_11[2]), .in_1(in_3), .in_2(in_8), .carry_in(fa_4_carry_out));
  fa fa_4 (.carry_out(fa_4_carry_out), .answer(out_11[1]), .in_1(in_4), .in_2(in_9), .carry_in(fa_5_carry_out));
  fa fa_5 (.carry_out(fa_5_carry_out), .answer(out_11[0]), .in_1(in_5), .in_2(in_10), .carry_in(1'b0));
endmodule

module ha (
  input  in_1,
  input  in_2,
  output R,
  output C
);

  xor xor_1 (R, in_1, in_2);
  and and_1 (C, in_2, in_1);
endmodule

module fa (
  input  in_1,
  input  in_2,
  input  carry_in,
  output carry_out,
  output answer
);

  wire ha_1_c, ha_1_r, ha_2_c;

  ha ha_1 (.R(ha_1_r), .C(ha_1_c), .in_1(in_2), .in_2(in_1));
  ha ha_2 (.R(answer), .C(ha_2_c), .in_1(ha_1_r), .in_2(carry_in));
  or or_1 (carry_out, ha_1_c, ha_2_c);
endmodule
