// Logisim project guia0802.circ as structural Verilog: 3 circuits, main circuit main
module main (
  input  in_1,
  input  in_2,
  input  in_3,
  input  in_4,
  input  in_5,
  input  in_6,
  input  in_7,
  input  in_8,
  input  in_9,
  input  in_10,
  output [5:0] out_11
);

  wire fs_2_borrow_out, fs_3_borrow_out, fs_4_borrow_out, fs_5_borrow_out;

  fs fs_1 (.borrow_out(out_11[5]), .answer(out_11[4]), .in_1(in_1), .in_2(in_6), .borrow_in(fs_2_borrow_out));
  fs fs_2 (.borrow_out(fs_2_borrow_out), .answer(out_11[3]), .in_1(in_2), .in_2(in_7), .borrow_in(fs_4_borrow_out));
  fs fs_3 (.borrow_out(fs_3_borrow_out), .answer(out_11[1]), .in_1(in_4), .in_2(in_9), .borrow_in(fs_5_borrow_out));
  fs fs_4 (.borrow_out(fs_4_borrow_out), .answer(out_11[2]), .in_1(in_3), .in_2(in_8), .borrow_in(fs_3_borrow_out));
  fs fs_5 (.borrow_out(fs_5_borrow_out), .answer(out_11[0]), .in_1(in_5), .in_2(in_10), .borrow_in(1'b0));
endmodule

module hs (
  input  in_1,
  input  in_2,
  output R,
  output C
);

  wire not_1_out;

  not not_1 (not_1_out, in_1);
  xor xor_1 (R, in_1, in_2);
  and and_1 (C, in_2, not_1_out);
endmodule

module fs (
  input  in_1,
  input  in_2,
  input  borrow_in,
  output borrow_out,
  output answer
);

  wire hs_1_c, hs_1_r, hs_2_c;

  hs hs_1 (.R(hs_1_r), .C(hs_1_c), .in_1(in_1), .in_2(in_2));
  hs hs_2 (.R(answer), .C(hs_2_c), .in_1(hs_1_r), .in_2(borrow_in));
  or or_1 (borrow_out, hs_1_c, hs_2_c);
endmodule
