// Logisim project guia0803.circ as structural Verilog: 1 circuit, main circuit main
module main (
  input  [5:0] in_1,
  input  [5:0] in_2,
  output out_3
);

  wire xnor_1_out, xnor_2_out, xnor_3_out, xnor_4_out, xnor_5_out, xnor_6_out;

  xnor xnor_1 (xnor_1_out, in_1[0], in_2[0]);
  xnor xnor_2 (xnor_2_out, in_1[1], in_2[1]);
  xnor xnor_3 (xnor_3_out, in_1[2], in_2[2]);
  xnor xnor_4 (xnor_4_out, in_1[3], in_2[3]);
  xnor xnor_5 (xnor_5_out, in_1[4], in_2[4]);
  xnor xnor_6 (xnor_6_out, in_1[5], in_2[5]);
  and and_1 (out_3, xnor_1_out, xnor_2_out, xnor_3_out, xnor_4_out, xnor_5_out, xnor_6_out);
endmodule
