// Logisim project guia0804.circ as structural Verilog: 1 circuit, main circuit main
module main (
  input  [5:0] in_1,
  input  [5:0] in_2,
  output out_3
);

  wire xor_1_out, xor_2_out, xor_3_out, xor_4_out, xor_5_out, xor_6_out;

  xor xor_1 (xor_1_out, in_1[0], in_2[0]);
  xor xor_2 (xor_2_out, in_1[1], in_2[1]);
  xor xor_3 (xor_3_out, in_1[2], in_2[2]);
  xor xor_4 (xor_4_out, in_1[3], in_2[3]);
  xor xor_5 (xor_5_out, in_1[4], in_2[4]);
  xor xor_6 (xor_6_out, in_1[5], in_2[5]);
  or or_1 (out_3, xor_1_out, xor_2_out, xor_3_out, xor_4_out, xor_5_out, xor_6_out);
endmodule
