// Logisim project guia0805.circ as structural Verilog
module c2 (
  input  [4:0] in_1,
  output [5:0] out_2
);

  wire ha_1_c, ha_3_c, ha_4_c, ha_5_c, not_1_out, not_2_out, not_3_out, not_4_out, not_5_out;

  ha ha_1 (.R(out_2[3]), .C(ha_1_c), .in_1(not_2_out), .in_2(ha_5_c));
  ha ha_2 (.R(out_2[4]), .C(out_2[5]), .in_1(not_3_out), .in_2(ha_1_c));
  not not_1 (not_1_out, in_1[0]);
  not not_2 (not_2_out, in_1[3]);
  not not_3 (not_3_out, in_1[4]);
  not not_4 (not_4_out, in_1[1]);
  not not_5 (not_5_out, in_1[2]);
  ha ha_3 (.R(out_2[0]), .C(ha_3_c), .in_1(not_1_out), .in_2(1'b1));
  ha ha_4 (.R(out_2[1]), .C(ha_4_c), .in_1(not_4_out), .in_2(ha_3_c));
  ha ha_5 (.R(out_2[2]), .C(ha_5_c), .in_1(not_5_out), .in_2(ha_4_c));
endmodule

module ha (
  input  in_1,
  input  in_2,
  output R,
  output C
);

  xor xor_1 (R, in_1, in_2);
  and and_1 (C, in_2, in_1);
endmodule

module fa (
  input  in_1,
  input  in_2,
  input  carry_in,
  output carry_out,
  output answer
);

  wire ha_1_c, ha_1_r, ha_2_c;

  ha ha_1 (.R(ha_1_r), .C(ha_1_c), .in_1(in_1), .in_2(in_2));
  ha ha_2 (.R(answer), .C(ha_2_c), .in_1(carry_in), .in_2(ha_1_r));
  or or_1 (carry_out, ha_1_c, ha_2_c);
endmodule

module fa_2 (
  input  [1:0] in_1,
  input  [1:0] in_2,
  input  carry_in,
  output carry_out,
  output [1:0] result
);

  wire fa_2_carry_out;

  fa fa_1 (.carry_out(carry_out), .answer(result[1]), .in_1(in_1[1]), .in_2(in_2[1]), .carry_in(fa_2_carry_out));
  fa fa_2 (.carry_out(fa_2_carry_out), .answer(result[0]), .in_1(in_1[0]), .in_2(in_2[0]), .carry_in(carry_in));
endmodule
