// Logisim project guia0806.circ as structural Verilog: 5 circuits, main circuit main
module main (
  input  [4:0] in_1,
  input  key,
  input  [4:0] in_3,
  output [5:0] out_4
);

  wire fa_4_1_out_4;
  wire [4:0] multiplexer_1_out, not_1_out;

  fa_4 fa_4_1 (.carry_in(key), .out_5(out_4[3:0]), .a(in_3[3:0]), .b(multiplexer_1_out[3:0]), .out_4(fa_4_1_out_4));
  fa fa_1 (.carry_out(out_4[5]), .answer(out_4[4]), .a(in_3[4]), .b(multiplexer_1_out[4]), .carry_in(fa_4_1_out_4));
  assign not_1_out = ~in_1;  // NOT_Gate not_1, 5 bits wide
  Multiplexer #(.width(5), .enable("false")) multiplexer_1 (
    .in0(in_1), .in1(not_1_out), .out(multiplexer_1_out), .sel(key));
endmodule

module ha (
  input  a,
  input  b,
  output R,
  output C
);

  xor xor_1 (R, a, b);
  and and_1 (C, b, a);
endmodule

module fa (
  input  a,
  input  b,
  input  carry_in,
  output carry_out,
  output answer
);

  wire ha_1_c, ha_1_r, ha_2_c;

  ha ha_1 (.R(ha_1_r), .C(ha_1_c), .a(a), .b(b));
  ha ha_2 (.R(answer), .C(ha_2_c), .a(carry_in), .b(ha_1_r));
  or or_1 (carry_out, ha_1_c, ha_2_c);
endmodule

module fa_2 (
  input  [1:0] a,
  input  [1:0] b,
  input  carry_in,
  output carry_out,
  output [1:0] result
);

  wire fa_2_carry_out;

  fa fa_1 (.carry_out(carry_out), .answer(result[1]), .a(a[1]), .b(b[1]), .carry_in(fa_2_carry_out));
  fa fa_2 (.carry_out(fa_2_carry_out), .answer(result[0]), .a(a[0]), .b(b[0]), .carry_in(carry_in));
endmodule

module fa_4 (
  input  [3:0] a,
  input  [3:0] b,
  input  carry_in,
  output out_4,
  output [3:0] out_5
);

  wire fa_2_2_carry_out;

  fa_2 fa_2_1 (.a(a[3:2]), .b(b[3:2]), .carry_out(out_4), .result(out_5[3:2]), .carry_in(fa_2_2_carry_out));
  fa_2 fa_2_2 (.a(a[1:0]), .b(b[1:0]), .carry_out(fa_2_2_carry_out), .result(out_5[1:0]), .carry_in(carry_in));
endmodule
