// Logisim project guia0807.circ as structural Verilog: 3 circuits, main circuit main
module main (
  input  [5:0] in_1,
  input  [5:0] in_2,
  input  in_3,
  output out_4
);

  wire different_1_out_3, equals_1_out_3;

  equals equals_1 (.in_1(in_1), .in_2(in_2), .out_3(equals_1_out_3));
  different different_1 (.in_1(in_1), .in_2(in_2), .out_3(different_1_out_3));
  Multiplexer #(.enable("false")) multiplexer_1 (
    .in0(equals_1_out_3), .in1(different_1_out_3), .out(out_4), .sel(in_3));
endmodule

module equals (
  input  [5:0] in_1,
  input  [5:0] in_2,
  output out_3
);

  wire xnor_1_out, xnor_2_out, xnor_3_out, xnor_4_out, xnor_5_out, xnor_6_out;

  xnor xnor_1 (xnor_1_out, in_1[0], in_2[0]);
  xnor xnor_2 (xnor_2_out, in_1[1], in_2[1]);
  xnor xnor_3 (xnor_3_out, in_1[2], in_2[2]);
  xnor xnor_4 (xnor_4_out, in_1[3], in_2[3]);
  xnor xnor_5 (xnor_5_out, in_1[4], in_2[4]);
  xnor xnor_6 (xnor_6_out, in_1[5], in_2[5]);
  and and_1 (out_3, xnor_1_out, xnor_2_out, xnor_3_out, xnor_4_out, xnor_5_out, xnor_6_out);
endmodule

module different (
  input  [5:0] in_1,
  input  [5:0] in_2,
  output out_3
);

  wire xor_1_out, xor_2_out, xor_3_out, xor_4_out, xor_5_out, xor_6_out;

  xor xor_1 (xor_1_out, in_1[0], in_2[0]);
  xor xor_2 (xor_2_out, in_1[1], in_2[1]);
  xor xor_3 (xor_3_out, in_1[2], in_2[2]);
  xor xor_4 (xor_4_out, in_1[3], in_2[3]);
  xor xor_5 (xor_5_out, in_1[4], in_2[4]);
  xor xor_6 (xor_6_out, in_1[5], in_2[5]);
  or or_1 (out_3, xor_1_out, xor_2_out, xor_3_out, xor_4_out, xor_5_out, xor_6_out);
endmodule
