// Logisim project prep2log.circ as structural Verilog: 5 circuits, main circuit jkff
module jkff (
  input  c,
  input  clear
);

  wire a_q, a_qn, and_1_out, and_2_out, and_3_out, and_4_out, b_q, b_qn, clock_1_out;

  Clock clock_1 (.out(clock_1_out));
  and and_1 (and_1_out, b_qn, c);
  and and_2 (and_2_out, c, b_q);
  // Probe on a_q
  J_K_Flip_Flop a (.J(and_1_out), .clk(clock_1_out), .K(and_2_out), .Q(a_q), .Qn(a_qn), .reset(clear));  // open: preset
  and and_3 (and_3_out, c, a_q);
  and and_4 (and_4_out, c, a_qn);
  // Probe on b_q
  J_K_Flip_Flop b (.J(and_3_out), .clk(clock_1_out), .K(and_4_out), .Q(b_q), .Qn(b_qn), .reset(clear));  // open: preset
endmodule

module dff (
  input  c,
  input  clear
);

  wire a_q, and_1_out, and_2_out, and_3_out, and_4_out, b_q, b_qn, clock_1_out, not_1_out, or_1_out, or_2_out;

  Clock clock_1 (.out(clock_1_out));
  not not_1 (not_1_out, c);
  and and_1 (and_1_out, not_1_out, a_q);
  and and_2 (and_2_out, c, b_qn);
  or or_1 (or_1_out, and_1_out, and_2_out);
  // Probe on a_q
  D_Flip_Flop a (.clk(clock_1_out), .D(or_1_out), .Q(a_q), .reset(clear));  // open: Qn, preset
  and and_3 (and_3_out, c, a_q);
  or or_2 (or_2_out, and_3_out, and_4_out);
  and and_4 (and_4_out, not_1_out, b_q);
  // Probe on b_q
  D_Flip_Flop b (.clk(clock_1_out), .D(or_2_out), .Q(b_q), .Qn(b_qn), .reset(clear));  // open: preset
endmodule

module tff (
  input  c,
  input  clear
);

  wire and_1_out, and_2_out, and_3_out, and_4_out, clock_1_out, or_1_out, or_2_out, t_ff_1_q, t_ff_1_qn,
       t_ff_2_q, t_ff_2_qn;

  Clock clock_1 (.out(clock_1_out));
  // NOT_Gate not_1 has open pins: in=c, out=open
  and and_1 (and_1_out, t_ff_2_qn, t_ff_1_qn, c);
  or or_1 (or_1_out, and_1_out, and_2_out);
  and and_2 (and_2_out, t_ff_1_q, t_ff_2_q, c);
  // Probe on t_ff_1_q
  T_Flip_Flop t_ff_1 (.clk(clock_1_out), .T(or_1_out), .Q(t_ff_1_q), .Qn(t_ff_1_qn), .reset(clear));  // open: preset
  and and_3 (and_3_out, t_ff_1_q, t_ff_2_qn, c);
  and and_4 (and_4_out, t_ff_1_qn, t_ff_2_q, c);
  // Probe on t_ff_2_q
  T_Flip_Flop t_ff_2 (.clk(clock_1_out), .T(or_2_out), .Q(t_ff_2_q), .Qn(t_ff_2_qn), .reset(clear));  // open: preset
  or or_2 (or_2_out, and_3_out, and_4_out);
endmodule

module sr (
  input  [3:0] load_data,
  input  load,
  input  clear
);

  wire and_1_out, and_2_out, and_3_out, and_4_out, clock_1_out, d_ff_1_q, d_ff_2_q, d_ff_3_q, d_ff_4_q;

  Clock clock_1 (.out(clock_1_out));
  // Probe on d_ff_1_q
  and and_1 (and_1_out, load, load_data[3]);
  D_Flip_Flop d_ff_1 (.clk(clock_1_out), .D(1'b0), .Q(d_ff_1_q), .preset(and_1_out), .reset(clear));  // open: Qn
  // Probe on d_ff_2_q
  and and_2 (and_2_out, load, load_data[2]);
  D_Flip_Flop d_ff_2 (.clk(clock_1_out), .D(d_ff_1_q), .Q(d_ff_2_q), .preset(and_2_out), .reset(clear));  // open: Qn
  and and_3 (and_3_out, load, load_data[1]);
  and and_4 (and_4_out, load, load_data[0]);
  // Probe on d_ff_3_q
  D_Flip_Flop d_ff_3 (.clk(clock_1_out), .D(d_ff_2_q), .Q(d_ff_3_q), .preset(and_3_out), .reset(clear));  // open: Qn
  // Probe on d_ff_4_q
  D_Flip_Flop d_ff_4 (.clk(clock_1_out), .D(d_ff_3_q), .Q(d_ff_4_q), .preset(and_4_out), .reset(clear));  // open: Qn
endmodule

module sl (
  input  [3:0] load_data,
  input  load,
  input  clear
);

  wire and_1_out, and_2_out, and_3_out, and_4_out, clock_1_out, d_ff_1_q, d_ff_2_q, d_ff_3_q, d_ff_4_q;

  Clock clock_1 (.out(clock_1_out));
  // Probe on d_ff_1_q
  and and_1 (and_1_out, load, load_data[3]);
  D_Flip_Flop d_ff_1 (.clk(clock_1_out), .D(d_ff_2_q), .Q(d_ff_1_q), .preset(and_1_out), .reset(clear));  // open: Qn
  and and_2 (and_2_out, load, load_data[2]);
  // Probe on d_ff_2_q
  and and_3 (and_3_out, load, load_data[1]);
  D_Flip_Flop d_ff_2 (.clk(clock_1_out), .D(d_ff_3_q), .Q(d_ff_2_q), .preset(and_2_out), .reset(clear));  // open: Qn
  // Probe on d_ff_3_q
  and and_4 (and_4_out, load, load_data[0]);
  D_Flip_Flop d_ff_3 (.clk(clock_1_out), .D(d_ff_4_q), .Q(d_ff_3_q), .preset(and_3_out), .reset(clear));  // open: Qn
  // Probe on d_ff_4_q
  D_Flip_Flop d_ff_4 (.clk(clock_1_out), .D(1'b0), .Q(d_ff_4_q), .preset(and_4_out), .reset(clear));  // open: Qn
endmodule
