// Logisim project rec0101.circ as structural Verilog: 6 circuits, main circuit sop
module sop (
  input  a,
  input  b,
  input  c,
  input  d,
  output s
);

  wire and_1_out, and_2_out, and_3_out, and_4_out, and_5_out, and_6_out, and_7_out, and_8_out, and_9_out,
       not_1_out, not_2_out, not_3_out, not_4_out, not_5_out, not_6_out, not_7_out, not_8_out, not_9_out,
       not_10_out, not_11_out, not_12_out, not_13_out, not_14_out, not_15_out;

  not not_1 (not_1_out, a);
  not not_2 (not_2_out, b);
  not not_3 (not_3_out, c);
  not not_4 (not_4_out, a);
  not not_5 (not_5_out, b);
  not not_6 (not_6_out, a);
  not not_7 (not_7_out, c);
  not not_8 (not_8_out, d);
  not not_9 (not_9_out, a);
  not not_10 (not_10_out, c);
  not not_11 (not_11_out, a);
  not not_12 (not_12_out, b);
  not not_13 (not_13_out, d);
  not not_14 (not_14_out, b);
  not not_15 (not_15_out, c);
  and and_1 (and_1_out, not_1_out, not_2_out, not_3_out, d);
  and and_2 (and_2_out, not_4_out, not_5_out, c, d);
  and and_3 (and_3_out, not_6_out, b, not_7_out, not_8_out);
  and and_4 (and_4_out, not_9_out, b, not_10_out, d);
  and and_5 (and_5_out, not_11_out, b, c, d);
  and and_6 (and_6_out, a, not_12_out, c, not_13_out);
  and and_7 (and_7_out, a, not_14_out, c, d);
  and and_8 (and_8_out, a, b, not_15_out, d);
  and and_9 (and_9_out, a, b, c, d);
  or or_1 (s, and_1_out, and_2_out, and_3_out, and_4_out, and_5_out, and_6_out, and_7_out, and_8_out, and_9_out);
endmodule

module sopm (
  input  a,
  input  b,
  input  c,
  input  d,
  output s
);

  wire and_1_out, and_2_out, and_3_out, and_4_out, not_1_out, not_2_out, not_3_out, not_4_out;

  not not_1 (not_1_out, a);
  and and_1 (and_1_out, not_1_out, b, not_2_out);
  not not_2 (not_2_out, c);
  not not_3 (not_3_out, a);
  and and_2 (and_2_out, not_3_out, d);
  and and_3 (and_3_out, b, d);
  not not_4 (not_4_out, b);
  and and_4 (and_4_out, a, not_4_out, c);
  or or_1 (s, and_1_out, and_2_out, and_3_out, and_4_out);
endmodule

module sopn (
  input  a,
  input  b,
  input  c,
  input  d,
  output s
);

  wire nand_1_out, nand_2_out, nand_3_out, nand_4_out, nand_5_out, nand_6_out, nand_7_out, nand_8_out,
       nand_9_out, nand_10_out, nand_11_out, nand_12_out, nand_13_out, nand_14_out, nand_15_out, nand_16_out,
       nand_17_out, nand_18_out, nand_19_out, nand_20_out, nand_21_out, nand_22_out, nand_23_out,
       nand_24_out, nand_25_out, nand_26_out, nand_27_out, nand_28_out, nand_29_out, nand_30_out,
       nand_31_out, nand_32_out, nand_33_out, nand_34_out, nand_35_out, nand_36_out, nand_37_out,
       nand_38_out, nand_39_out, nand_40_out, nand_41_out, nand_42_out, nand_43_out, nand_44_out,
       nand_45_out, nand_46_out, nand_47_out, nand_48_out, nand_49_out, nand_50_out, nand_51_out,
       nand_52_out, nand_53_out, nand_54_out, nand_55_out, nand_56_out, nand_57_out, nand_58_out,
       nand_59_out, nand_60_out, nand_61_out, nand_62_out, nand_63_out, nand_64_out, nand_65_out,
       nand_66_out, nand_67_out, nand_68_out, nand_69_out, nand_70_out, nand_71_out, nand_72_out,
       nand_73_out, nand_74_out;

  nand nand_1 (nand_1_out, a, a);
  nand nand_2 (nand_2_out, b, b);
  nand nand_3 (nand_3_out, c, c);
  nand nand_4 (nand_4_out, a, a);
  nand nand_5 (nand_5_out, b, b);
  nand nand_6 (nand_6_out, nand_1_out, nand_2_out);
  nand nand_7 (nand_7_out, nand_3_out, d);
  nand nand_8 (nand_8_out, nand_4_out, nand_5_out);
  nand nand_9 (nand_9_out, c, d);
  nand nand_10 (nand_10_out, nand_6_out, nand_6_out);
  nand nand_11 (nand_11_out, nand_7_out, nand_7_out);
  nand nand_12 (nand_12_out, nand_8_out, nand_8_out);
  nand nand_13 (nand_13_out, nand_9_out, nand_9_out);
  nand nand_14 (nand_14_out, a, a);
  nand nand_15 (nand_15_out, c, c);
  nand nand_16 (nand_16_out, d, d);
  nand nand_17 (nand_17_out, a, a);
  nand nand_18 (nand_18_out, c, c);
  nand nand_19 (nand_19_out, a, a);
  nand nand_20 (nand_20_out, b, b);
  nand nand_21 (nand_21_out, d, d);
  nand nand_22 (nand_22_out, b, b);
  nand nand_23 (nand_23_out, c, c);
  nand nand_24 (nand_24_out, nand_10_out, nand_11_out);
  nand nand_25 (nand_25_out, nand_12_out, nand_13_out);
  nand nand_26 (nand_26_out, nand_14_out, b);
  nand nand_27 (nand_27_out, nand_15_out, nand_16_out);
  nand nand_28 (nand_28_out, nand_17_out, b);
  nand nand_29 (nand_29_out, nand_18_out, d);
  nand nand_30 (nand_30_out, nand_19_out, b);
  nand nand_31 (nand_31_out, c, d);
  nand nand_32 (nand_32_out, a, nand_20_out);
  nand nand_33 (nand_33_out, c, nand_21_out);
  nand nand_34 (nand_34_out, a, nand_22_out);
  nand nand_35 (nand_35_out, c, d);
  nand nand_36 (nand_36_out, a, b);
  nand nand_37 (nand_37_out, nand_23_out, d);
  nand nand_38 (nand_38_out, a, b);
  nand nand_39 (nand_39_out, c, d);
  nand nand_40 (nand_40_out, nand_24_out, nand_25_out);
  nand nand_41 (nand_41_out, nand_26_out, nand_26_out);
  nand nand_42 (nand_42_out, nand_27_out, nand_27_out);
  nand nand_43 (nand_43_out, nand_28_out, nand_28_out);
  nand nand_44 (nand_44_out, nand_29_out, nand_29_out);
  nand nand_45 (nand_45_out, nand_30_out, nand_30_out);
  nand nand_46 (nand_46_out, nand_31_out, nand_31_out);
  nand nand_47 (nand_47_out, nand_32_out, nand_32_out);
  nand nand_48 (nand_48_out, nand_33_out, nand_33_out);
  nand nand_49 (nand_49_out, nand_34_out, nand_34_out);
  nand nand_50 (nand_50_out, nand_35_out, nand_35_out);
  nand nand_51 (nand_51_out, nand_36_out, nand_36_out);
  nand nand_52 (nand_52_out, nand_37_out, nand_37_out);
  nand nand_53 (nand_53_out, nand_38_out, nand_38_out);
  nand nand_54 (nand_54_out, nand_39_out, nand_39_out);
  nand nand_55 (nand_55_out, nand_40_out, nand_40_out);
  nand nand_56 (nand_56_out, nand_41_out, nand_42_out);
  nand nand_57 (nand_57_out, nand_43_out, nand_44_out);
  nand nand_58 (nand_58_out, nand_45_out, nand_46_out);
  nand nand_59 (nand_59_out, nand_47_out, nand_48_out);
  nand nand_60 (nand_60_out, nand_49_out, nand_50_out);
  nand nand_61 (nand_61_out, nand_51_out, nand_52_out);
  nand nand_62 (nand_62_out, nand_53_out, nand_54_out);
  nand nand_63 (nand_63_out, nand_55_out, nand_56_out);
  nand nand_64 (nand_64_out, nand_57_out, nand_58_out);
  nand nand_65 (nand_65_out, nand_59_out, nand_60_out);
  nand nand_66 (nand_66_out, nand_61_out, nand_62_out);
  nand nand_67 (nand_67_out, nand_63_out, nand_63_out);
  nand nand_68 (nand_68_out, nand_64_out, nand_64_out);
  nand nand_69 (nand_69_out, nand_65_out, nand_65_out);
  nand nand_70 (nand_70_out, nand_66_out, nand_66_out);
  nand nand_71 (nand_71_out, nand_67_out, nand_68_out);
  nand nand_72 (nand_72_out, nand_69_out, nand_70_out);
  nand nand_73 (nand_73_out, nand_71_out, nand_71_out);
  nand nand_74 (nand_74_out, nand_72_out, nand_72_out);
  nand nand_75 (s, nand_73_out, nand_74_out);
endmodule

module pos (
  input  A,
  input  B,
  input  C,
  input  D,
  output s
);

  wire not_1_out, not_2_out, not_3_out, not_4_out, not_5_out, not_6_out, not_7_out, not_8_out, not_9_out,
       not_10_out, not_11_out, or_1_out, or_2_out, or_3_out, or_4_out, or_5_out, or_6_out, or_7_out;

  not not_1 (not_1_out, C);
  not not_2 (not_2_out, B);
  not not_3 (not_3_out, C);
  not not_4 (not_4_out, A);
  not not_5 (not_5_out, A);
  not not_6 (not_6_out, D);
  not not_7 (not_7_out, A);
  not not_8 (not_8_out, B);
  not not_9 (not_9_out, A);
  not not_10 (not_10_out, B);
  not not_11 (not_11_out, C);
  or or_1 (or_1_out, A, B, C, D);
  or or_2 (or_2_out, A, B, not_1_out, D);
  or or_3 (or_3_out, A, not_2_out, not_3_out, D);
  or or_4 (or_4_out, not_4_out, B, C, D);
  or or_5 (or_5_out, not_5_out, B, C, not_6_out);
  or or_6 (or_6_out, not_7_out, not_8_out, C, D);
  or or_7 (or_7_out, not_9_out, not_10_out, not_11_out, D);
  and and_1 (s, or_1_out, or_2_out, or_3_out, or_4_out, or_5_out, or_6_out, or_7_out);
endmodule

module posm (
  input  A,
  input  B,
  input  C,
  input  D,
  output s
);

  wire not_1_out, not_2_out, not_3_out, not_4_out, or_1_out, or_2_out, or_3_out, or_4_out;

  or or_1 (or_1_out, A, B, D);
  not not_1 (not_1_out, B);
  or or_2 (or_2_out, not_1_out, not_2_out, D);
  not not_2 (not_2_out, C);
  not not_3 (not_3_out, A);
  or or_3 (or_3_out, not_3_out, C, D);
  not not_4 (not_4_out, A);
  or or_4 (or_4_out, not_4_out, B, C);
  and and_1 (s, or_1_out, or_2_out, or_3_out, or_4_out);
endmodule

module posn (
  input  A,
  input  B,
  input  C,
  input  D,
  output s
);

  wire nor_1_out, nor_2_out, nor_3_out, nor_4_out, nor_5_out, nor_6_out, nor_7_out, nor_8_out, nor_9_out,
       nor_10_out, nor_11_out, nor_12_out, nor_13_out, nor_14_out, nor_15_out, nor_16_out, nor_17_out,
       nor_18_out, nor_19_out, nor_20_out, nor_21_out, nor_22_out, nor_23_out, nor_24_out, nor_25_out,
       nor_26_out, nor_27_out, nor_28_out, nor_29_out, nor_30_out, nor_31_out, nor_32_out, nor_33_out,
       nor_34_out, nor_35_out, nor_36_out, nor_37_out, nor_38_out, nor_39_out, nor_40_out, nor_41_out,
       nor_42_out, nor_43_out, nor_44_out, nor_45_out, nor_46_out, nor_47_out, nor_48_out, nor_49_out,
       nor_50_out, nor_51_out, nor_52_out, nor_53_out, not_1_out, not_2_out, not_3_out;

  nor nor_1 (nor_1_out, C, C);
  nor nor_2 (nor_2_out, B, B);
  nor nor_3 (nor_3_out, C, C);
  nor nor_4 (nor_4_out, A, A);
  nor nor_5 (nor_5_out, A, A);
  nor nor_6 (nor_6_out, D, D);
  nor nor_7 (nor_7_out, A, A);
  nor nor_8 (nor_8_out, B, B);
  not not_1 (not_1_out, A);
  not not_2 (not_2_out, B);
  not not_3 (not_3_out, C);
  nor nor_9 (nor_9_out, nor_10_out, nor_10_out);
  nor nor_10 (nor_10_out, A, B);
  nor nor_11 (nor_11_out, C, D);
  nor nor_12 (nor_12_out, nor_11_out, nor_11_out);
  nor nor_13 (nor_13_out, A, B);
  nor nor_14 (nor_14_out, nor_13_out, nor_13_out);
  nor nor_15 (nor_15_out, nor_1_out, D);
  nor nor_16 (nor_16_out, nor_15_out, nor_15_out);
  nor nor_17 (nor_17_out, nor_18_out, nor_18_out);
  nor nor_18 (nor_18_out, A, nor_2_out);
  nor nor_19 (nor_19_out, nor_20_out, nor_20_out);
  nor nor_20 (nor_20_out, nor_3_out, D);
  nor nor_21 (nor_21_out, nor_4_out, B);
  nor nor_22 (nor_22_out, nor_21_out, nor_21_out);
  nor nor_23 (nor_23_out, nor_24_out, nor_24_out);
  nor nor_24 (nor_24_out, C, D);
  nor nor_25 (nor_25_out, nor_26_out, nor_26_out);
  nor nor_26 (nor_26_out, nor_5_out, B);
  nor nor_27 (nor_27_out, C, nor_6_out);
  nor nor_28 (nor_28_out, nor_27_out, nor_27_out);
  nor nor_29 (nor_29_out, nor_30_out, nor_30_out);
  nor nor_30 (nor_30_out, nor_7_out, nor_8_out);
  nor nor_31 (nor_31_out, C, D);
  nor nor_32 (nor_32_out, nor_31_out, nor_31_out);
  nor nor_33 (nor_33_out, not_1_out, not_2_out);
  nor nor_34 (nor_34_out, not_3_out, D);
  nor nor_35 (nor_35_out, nor_9_out, nor_12_out);
  nor nor_36 (nor_36_out, nor_14_out, nor_16_out);
  nor nor_37 (nor_37_out, nor_17_out, nor_19_out);
  nor nor_38 (nor_38_out, nor_22_out, nor_23_out);
  nor nor_39 (nor_39_out, nor_25_out, nor_28_out);
  nor nor_40 (nor_40_out, nor_29_out, nor_32_out);
  nor nor_41 (nor_41_out, nor_33_out, nor_33_out);
  nor nor_42 (nor_42_out, nor_34_out, nor_34_out);
  nor nor_43 (nor_43_out, nor_35_out, nor_36_out);
  nor nor_44 (nor_44_out, nor_37_out, nor_38_out);
  nor nor_45 (nor_45_out, nor_39_out, nor_40_out);
  nor nor_46 (nor_46_out, nor_41_out, nor_42_out);
  nor nor_47 (nor_47_out, nor_43_out, nor_43_out);
  nor nor_48 (nor_48_out, nor_44_out, nor_44_out);
  nor nor_49 (nor_49_out, nor_45_out, nor_45_out);
  nor nor_50 (nor_50_out, nor_49_out, nor_46_out);
  nor nor_51 (nor_51_out, nor_52_out, nor_52_out);
  nor nor_52 (nor_52_out, nor_47_out, nor_48_out);
  nor nor_53 (nor_53_out, nor_50_out, nor_50_out);
  nor nor_54 (s, nor_51_out, nor_53_out);
endmodule
