// Logisim project rec0102.circ as structural Verilog: 2 circuits, main circuit letterA
module letterA (
  input  a,
  input  b,
  output out_3
);

  wire not_1_out;

  not not_1 (not_1_out, b);
  Multiplexer #(.enable("false")) multiplexer_1 (.in0(not_1_out), .in1(b), .out(out_3), .sel(a));
endmodule

module letterB (
  input  a,
  input  b,
  input  c,
  output out_4
);

  wire nand_1_out, nand_2_out, nand_3_out, nand_4_out;

  nand nand_1 (nand_1_out, a, a);
  nand nand_2 (nand_2_out, b, b);
  nand nand_3 (nand_3_out, nand_1_out, b);
  nand nand_4 (nand_4_out, nand_2_out, c);
  nand nand_5 (out_4, nand_3_out, nand_4_out);
endmodule
