// Logisim project rec0103.circ as structural Verilog: 2 circuits, main circuit letterA
module letterA (
  input  a,
  input  b,
  input  d,
  output s
);

  wire and_1_out, and_2_out, not_1_out, not_2_out;

  not not_1 (not_1_out, a);
  not not_2 (not_2_out, b);
  and and_1 (and_1_out, not_1_out, d);
  and and_2 (and_2_out, a, not_2_out);
  or or_1 (s, and_1_out, and_2_out);
endmodule

module letterB (
  input  a,
  input  b,
  input  c,
  input  d,
  output s
);

  wire and_1_out, and_2_out, and_3_out, not_1_out, not_2_out, not_3_out;

  not not_1 (not_1_out, a);
  and and_1 (and_1_out, not_1_out, not_2_out, d);
  not not_2 (not_2_out, c);
  and and_2 (and_2_out, a, not_3_out);
  not not_3 (not_3_out, b);
  and and_3 (and_3_out, not_3_out, d);
  or or_1 (s, and_1_out, and_2_out, and_3_out);
endmodule
