// Logisim project rec0104.circ as structural Verilog: 2 circuits, main circuit letterA
module letterA (
  input  a,
  input  b,
  input  c,
  output s
);

  wire and_1_out, not_1_out;

  not not_1 (not_1_out, a);
  and and_1 (and_1_out, b, c);
  nor nor_1 (s, not_1_out, and_1_out);
endmodule

module letterB (
  input  a,
  input  b,
  input  c,
  output s
);

  wire nand_1_out, nand_2_out;

  nand nand_1 (nand_1_out, b, c);
  nand nand_2 (nand_2_out, a, nand_1_out);
  nand nand_3 (s, nand_2_out, nand_2_out);
endmodule
