// Logisim project Rec02_01.circ as structural Verilog: 3 circuits, main circuit a/b
module a_b (
  input  \event ,
  input  clear
);

  wire and_1_out, and_2_out, and_3_out, clock_out, d_ff_1_q, d_ff_1_qn, d_ff_2_q, d_ff_2_qn, not_1_out,
       or_1_out, or_2_out, or_3_out;

  Clock clock (.out(clock_out));
  or or_1 (or_1_out, and_2_out, and_1_out);
  not not_1 (not_1_out, \event );
  and and_1 (and_1_out, \event , d_ff_2_qn, d_ff_1_q);
  and and_2 (and_2_out, not_1_out, d_ff_2_q, d_ff_1_qn);
  // Probe on d_ff_1_q
  D_Flip_Flop d_ff_1 (.clk(clock_out), .D(or_1_out), .Q(d_ff_1_q), .Qn(d_ff_1_qn), .reset(clear));  // open: preset
  and and_3 (and_3_out, or_2_out, or_3_out);
  or or_2 (or_2_out, \event , d_ff_2_q);
  // Probe on d_ff_2_q
  D_Flip_Flop d_ff_2 (.clk(clock_out), .D(and_3_out), .Q(d_ff_2_q), .Qn(d_ff_2_qn), .reset(clear));  // open: preset
  or or_3 (or_3_out, d_ff_1_q, d_ff_2_qn);
endmodule

module c_d (
  input  \event ,
  input  clear
);

  wire and_1_out, and_2_out, clock_out, j_k_ff_1_q, j_k_ff_2_q, j_k_ff_2_qn, not_1_out, or_1_out, xor_1_out;

  Clock clock (.out(clock_out));
  not not_1 (not_1_out, \event );
  xor xor_1 (xor_1_out, j_k_ff_1_q, j_k_ff_2_q);
  and and_1 (and_1_out, xor_1_out, not_1_out);
  and and_2 (and_2_out, not_1_out, j_k_ff_2_qn);
  // Probe on j_k_ff_1_q
  J_K_Flip_Flop j_k_ff_1 (
    .J(and_1_out), .clk(clock_out), .K(and_2_out), .Q(j_k_ff_1_q), .reset(clear));  // open: Qn, preset
  or or_1 (or_1_out, \event , j_k_ff_2_q);
  // Probe on j_k_ff_2_q
  J_K_Flip_Flop j_k_ff_2 (
    .J(or_1_out), .clk(clock_out), .K(1'b1), .Q(j_k_ff_2_q), .Qn(j_k_ff_2_qn), .reset(clear));  // open: preset
endmodule

module e_f (
  input  \event ,
  input  clear
);

  wire and_1_out, clock_out, not_1_out, or_1_out, t_ff_1_q, t_ff_2_q, xor_1_out;

  Clock clock (.out(clock_out));
  not not_1 (not_1_out, \event );
  xor xor_1 (xor_1_out, not_1_out, t_ff_1_q);
  and and_1 (and_1_out, xor_1_out, t_ff_2_q);
  T_Flip_Flop t_ff_1 (.clk(clock_out), .T(and_1_out), .Q(t_ff_1_q), .reset(clear));  // open: Qn, preset
  or or_1 (or_1_out, \event , t_ff_2_q);
  T_Flip_Flop t_ff_2 (.clk(clock_out), .T(or_1_out), .Q(t_ff_2_q), .reset(clear));  // open: Qn, preset
endmodule
