// Logisim project Rec2_03.circ as structural Verilog: 1 circuit, main circuit main
module main (
  input  clear
);

  wire clk_out, j_k_ff_1_q, j_k_ff_2_q;

  Clock clk (.out(clk_out));
  // Probe on j_k_ff_1_q
  J_K_Flip_Flop j_k_ff_1 (.J(1'b1), .clk(clk_out), .K(1'b1), .Q(j_k_ff_1_q), .reset(clear));  // open: Qn, preset
  // Probe on j_k_ff_2_q
  J_K_Flip_Flop j_k_ff_2 (.J(1'b1), .clk(j_k_ff_1_q), .K(1'b1), .Q(j_k_ff_2_q), .reset(clear));  // open: Qn, preset
endmodule
