// Logisim project Rec2_05.circ as structural Verilog: 1 circuit, main circuit main
module main (
  input  clear
);

  wire clk_out, j_k_ff_1_q, j_k_ff_1_qn, j_k_ff_2_q, j_k_ff_2_qn;

  Clock clk (.out(clk_out));
  // Probe on j_k_ff_1_q
  J_K_Flip_Flop j_k_ff_1 (
    .J(j_k_ff_2_qn), .clk(clk_out), .K(j_k_ff_2_q), .Q(j_k_ff_1_q), .Qn(j_k_ff_1_qn), .reset(clear));  // open: preset
  // Probe on j_k_ff_2_q
  J_K_Flip_Flop j_k_ff_2 (
    .J(j_k_ff_1_q), .clk(clk_out), .K(j_k_ff_1_qn), .Q(j_k_ff_2_q), .Qn(j_k_ff_2_qn), .reset(clear));  // open: preset
endmodule
