// Logisim project Rec2_07.circ as structural Verilog: 1 circuit, main circuit main
module main (
  input  in_1,
  output [5:0] out_2
);

  wire and_1_out, clock_1_out, or_1_out, t_ff_1_qn, t_ff_2_qn, t_ff_3_qn, t_ff_4_qn, t_ff_5_qn;

  Clock clock_1 (.out(clock_1_out));
  T_Flip_Flop t_ff_1 (.clk(clock_1_out), .T(1'b1), .Q(out_2[0]), .Qn(t_ff_1_qn), .reset(or_1_out));  // open: preset
  or or_1 (or_1_out, in_1, and_1_out);
  and and_1 (and_1_out, out_2[0], t_ff_5_qn, t_ff_4_qn, t_ff_3_qn, t_ff_2_qn, out_2[5]);
  T_Flip_Flop t_ff_2 (.clk(t_ff_1_qn), .T(1'b1), .Q(out_2[1]), .Qn(t_ff_2_qn), .reset(or_1_out));  // open: preset
  T_Flip_Flop t_ff_3 (.clk(t_ff_2_qn), .T(1'b1), .Q(out_2[2]), .Qn(t_ff_3_qn), .reset(or_1_out));  // open: preset
  T_Flip_Flop t_ff_4 (.clk(t_ff_3_qn), .T(1'b1), .Q(out_2[3]), .Qn(t_ff_4_qn), .reset(or_1_out));  // open: preset
  T_Flip_Flop t_ff_5 (.clk(t_ff_4_qn), .T(1'b1), .Q(out_2[4]), .Qn(t_ff_5_qn), .reset(or_1_out));  // open: preset
  T_Flip_Flop t_ff_6 (.clk(t_ff_5_qn), .T(1'b1), .Q(out_2[5]), .reset(or_1_out));  // open: Qn, preset
endmodule
